// Logisim project Jean-Implementations.circ as structural Verilog: 8 circuits, main circuit main
module main (
  input  Start,
  input  CLK,
  input  CLR,
  input  R_W_Time_Selector,
  input  [3:0] Read_Time,
  input  [3:0] Write_Time,
  input  [31:0] Address_In,
  input  [31:0] Register,
  input  [31:0] RAM_out_0,
  input  [31:0] RAM_out_1,
  input  [31:0] RAM_out_2,
  input  [31:0] RAM_out_3,
  output [31:0] RAM_in_0,
  output [31:0] RAM_in_1,
  output [31:0] RAM_in_2,
  output [31:0] RAM_in_3,
  output [31:0] Out,
  output R_W,
  output End,
  output CS,
  output [3:0] RAM_massk,
  output [15:0] Address
);

  wire [31:0] demultiplexer_1_out1;

  Decoder #(.select(2), .enable("false")) decoder_1 (
    .out0(RAM_massk[0]), .out1(RAM_massk[1]), .out2(RAM_massk[2]), .out3(RAM_massk[3]), .sel(Address_In[3:2]));
  Multiplexer #(.select(2), .width(32), .enable("false")) multiplexer_1 (
    .in0(RAM_out_0), .in1(RAM_out_1), .in2(RAM_out_2), .in3(RAM_out_3),
    .out({Out[7:0], Out[15:8], Out[23:16], Out[31:24]}), .sel(Address_In[3:2]));
  Demultiplexer #(.width(32), .enable("false")) demultiplexer_1 (
    .out1(demultiplexer_1_out1), .in({Register[7:0], Register[15:8], Register[23:16], Register[31:24]}),
    .sel(R_W_Time_Selector));  // open: out0
  Demultiplexer #(.select(2), .width(32), .enable("false")) demultiplexer_2 (
    .out0(RAM_in_0), .out1(RAM_in_1), .out2(RAM_in_2), .out3(RAM_in_3), .in(demultiplexer_1_out1),
    .sel(Address_In[3:2]));

  assign Address = Address_In[19:4];
  assign CS = 1'b1;
  assign R_W = R_W_Time_Selector;

  // Other names for the same wires on the sheet: block[1:0] = Address_In[3:2]; ADDR[15:0] = Address_In[19:4];
  //   R_T[3:0] = Read_Time; R_W_TS = R_W_Time_Selector; RAM_input_1[31:0] = RAM_in_1; RAM_input_2[31:0] = RAM_in_2;
  //   RAM_input_3[31:0] = RAM_in_3; RAM_inputt_0[31:0] = RAM_in_0; RAM_mask[3:0] = RAM_massk; W_T[3:0] = Write_Time

  // Notes on the sheet:
  //   input
  //   output
endmodule

module Register_File (
  input  Clock,
  input  [4:0] Rs,
  input  [4:0] Rt,
  input  [4:0] Rd,
  input  [31:0] Write_Data,
  input  Reg_Write,
  input  Clear,
  output [31:0] Read_Data_1,
  output [31:0] Read_Data_2
);

  wire R0_Wreg, R1_Wreg, R2_Wreg, R3_Wreg, R4_Wreg, R5_Wreg, R6_Wreg, R7_Wreg, R8_Wreg, R9_Wreg, R10_Wreg,
       R11_Wreg, R12_Wreg, R13_Wreg, R14_Wreg, R15_Wreg, R16_Wreg, R17_Wreg, R18_Wreg, R19_Wreg, R20_Wreg,
       R21_Wreg, R22_Wreg, R23_Wreg, R24_Wreg, R25_Wreg, R26_Wreg, R27_Wreg, R28_Wreg, R29_Wreg, R30_Wreg,
       R31_Wreg;
  wire [31:0] R1, R2, R3, R4, R5, R6, R7, R8, R9, R10, R11, R12, R13, R14, R15, R16, R17, R18, R19, R20, R21,
       R22, R23, R24, R25, R26, R27, R28, R29, R30, R31;

  Multiplexer #(.select(5), .width(32)) multiplexer_1 (
    .in0({32{1'b0}}), .in1(R1), .in2(R2), .in3(R3), .in4(R4), .in5(R5), .in6(R6), .in7(R7), .in8(R8),
    .in9(R9), .in10(R10), .in11(R11), .in12(R12), .in13(R13), .in14(R14), .in15(R15), .in16(R16), .in17(R17),
    .in18(R18), .in19(R19), .in20(R20), .in21(R21), .in22(R22), .in23(R23), .in24(R24), .in25(R25),
    .in26(R26), .in27(R27), .in28(R28), .in29(R29), .in30(R30), .in31(R31), .out(Read_Data_1), .sel(Rs));  // open: en
  Multiplexer #(.select(5), .width(32)) multiplexer_2 (
    .in0({32{1'b0}}), .in1(R1), .in2(R2), .in3(R3), .in4(R4), .in5(R5), .in6(R6), .in7(R7), .in8(R8),
    .in9(R9), .in10(R10), .in11(R11), .in12(R12), .in13(R13), .in14(R14), .in15(R15), .in16(R16), .in17(R17),
    .in18(R18), .in19(R19), .in20(R20), .in21(R21), .in22(R22), .in23(R23), .in24(R24), .in25(R25),
    .in26(R26), .in27(R27), .in28(R28), .in29(R29), .in30(R30), .in31(R31), .out(Read_Data_2), .sel(Rt));  // open: en
  Decoder #(.select(5)) decoder_1 (
    .out0(R0_Wreg), .out1(R1_Wreg), .out2(R2_Wreg), .out3(R3_Wreg), .out4(R4_Wreg), .out5(R5_Wreg),
    .out6(R6_Wreg), .out7(R7_Wreg), .out8(R8_Wreg), .out9(R9_Wreg), .out10(R10_Wreg), .out11(R11_Wreg),
    .out12(R12_Wreg), .out13(R13_Wreg), .out14(R14_Wreg), .out15(R15_Wreg), .out16(R16_Wreg),
    .out17(R17_Wreg), .out18(R18_Wreg), .out19(R19_Wreg), .out20(R20_Wreg), .out21(R21_Wreg),
    .out22(R22_Wreg), .out23(R23_Wreg), .out24(R24_Wreg), .out25(R25_Wreg), .out26(R26_Wreg),
    .out27(R27_Wreg), .out28(R28_Wreg), .out29(R29_Wreg), .out30(R30_Wreg), .out31(R31_Wreg), .sel(Rd));  // open: en
  Register #(.width(32)) R (.D(Write_Data), .en(R1_Wreg), .Q(R1), .clk(Clock), .clr(Clear));
  Register #(.width(32)) R_2 (.D(Write_Data), .en(R2_Wreg), .Q(R2), .clk(Clock), .clr(Clear));
  Register #(.width(32)) R_3 (.D(Write_Data), .en(R3_Wreg), .Q(R3), .clk(Clock), .clr(Clear));
  Register #(.width(32)) R_4 (.D(Write_Data), .en(R4_Wreg), .Q(R4), .clk(Clock), .clr(Clear));
  Register #(.width(32)) R_5 (.D(Write_Data), .en(R5_Wreg), .Q(R5), .clk(Clock), .clr(Clear));
  Register #(.width(32)) R_6 (.D(Write_Data), .en(R6_Wreg), .Q(R6), .clk(Clock), .clr(Clear));
  Register #(.width(32)) R_7 (.D(Write_Data), .en(R7_Wreg), .Q(R7), .clk(Clock), .clr(Clear));
  Register #(.width(32)) R_8 (.D(Write_Data), .en(R8_Wreg), .Q(R8), .clk(Clock), .clr(Clear));
  Register #(.width(32)) R_9 (.D(Write_Data), .en(R9_Wreg), .Q(R9), .clk(Clock), .clr(Clear));
  Register #(.width(32)) R_10 (.D(Write_Data), .en(R10_Wreg), .Q(R10), .clk(Clock), .clr(Clear));
  Register #(.width(32)) R_11 (.D(Write_Data), .en(R11_Wreg), .Q(R11), .clk(Clock), .clr(Clear));
  Register #(.width(32)) R_12 (.D(Write_Data), .en(R12_Wreg), .Q(R12), .clk(Clock), .clr(Clear));
  Register #(.width(32)) R_13 (.D(Write_Data), .en(R13_Wreg), .Q(R13), .clk(Clock), .clr(Clear));
  Register #(.width(32)) R_14 (.D(Write_Data), .en(R14_Wreg), .Q(R14), .clk(Clock), .clr(Clear));
  Register #(.width(32)) R_15 (.D(Write_Data), .en(R15_Wreg), .Q(R15), .clk(Clock), .clr(Clear));
  Register #(.width(32)) R_16 (.D(Write_Data), .en(R16_Wreg), .Q(R16), .clk(Clock), .clr(Clear));
  Register #(.width(32)) R_17 (.D(Write_Data), .en(R17_Wreg), .Q(R17), .clk(Clock), .clr(Clear));
  Register #(.width(32)) R_18 (.D(Write_Data), .en(R18_Wreg), .Q(R18), .clk(Clock), .clr(Clear));
  Register #(.width(32)) R_19 (.D(Write_Data), .en(R19_Wreg), .Q(R19), .clk(Clock), .clr(Clear));
  Register #(.width(32)) R_20 (.D(Write_Data), .en(R20_Wreg), .Q(R20), .clk(Clock), .clr(Clear));
  Register #(.width(32)) R_21 (.D(Write_Data), .en(R21_Wreg), .Q(R21), .clk(Clock), .clr(Clear));
  Register #(.width(32)) R_22 (.D(Write_Data), .en(R23_Wreg), .Q(R22), .clk(Clock), .clr(Clear));
  Register #(.width(32)) R_23 (.D(Write_Data), .en(R23_Wreg), .Q(R23), .clk(Clock), .clr(Clear));
  Register #(.width(32)) R_24 (.D(Write_Data), .en(R24_Wreg), .Q(R24), .clk(Clock), .clr(Clear));
  Register #(.width(32)) R_25 (.D(Write_Data), .en(R25_Wreg), .Q(R25), .clk(Clock), .clr(Clear));
  Register #(.width(32)) R_26 (.D(Write_Data), .en(R26_Wreg), .Q(R26), .clk(Clock), .clr(Clear));
  Register #(.width(32)) R_27 (.D(Write_Data), .en(R27_Wreg), .Q(R27), .clk(Clock), .clr(Clear));
  Register #(.width(32)) R_28 (.D(Write_Data), .en(R28_Wreg), .Q(R28), .clk(Clock), .clr(Clear));
  Register #(.width(32)) R_29 (.D(Write_Data), .en(R29_Wreg), .Q(R29), .clk(Clock), .clr(Clear));
  Register #(.width(32)) R_30 (.D(Write_Data), .en(R30_Wreg), .Q(R30), .clk(Clock), .clr(Clear));
  Register #(.width(32)) R_31 (.D(Write_Data), .en(R31_Wreg), .Q(R31), .clk(Clock), .clr(Clear));

  // Other names for the same wires on the sheet: CLK = Clock; WData[31:0] = Write_Data; WReg = Reg_Write

  // Notes on the sheet:
  //   Registers
endmodule

module Instruction_Decoder (
  input  [31:0] Instruction,
  output nop,
  output tty,
  output mfhi,
  output mflo,
  output be,
  output halt,
  output rnd,
  output kbd,
  output j,
  output jr,
  output [27:0] destino,
  output [4:0] Rs,
  output pop,
  output push,
  output logic_i,
  output [4:0] Rt,
  output lw,
  output sw,
  output [4:0] Rd,
  output mul_div,
  output [3:0] alu_operator,
  output bne,
  output [31:0] Logic_Op,
  output [31:0] Aritmetic_Op,
  output [31:0] Branch,
  output load_zero,
  output blez,
  output [1:0] data_to_RF,
  output RF_zero,
  output pop_push,
  output bgtz,
  output load_Rd,
  output lw_sw,
  output inmediate,
  output bltz
);

  wire a, add, add_i, ai, \and , and_17_out, and_18_out, and_19_out, and_20_out, and_24_out, and_29_out,
       and_30_out, and_i, branch_t, div, div_u, func_code____0, func_code____1, func_code____011, mul, mul_u,
       \nor , op_code____0, op_code____1, opp_aritmetica, \or , or_3_out, or_9_out, or_10_out, or_11_out,
       or_12_out, or_13_out, or_14_out, or_15_out, or_i, slt, slt_i, slt_u, sltu_i, sub, \xor , xor_i;

  and and_1 (func_code____1, Instruction[0], Instruction[1], Instruction[3], Instruction[4], Instruction[5]);
  and and_2 (func_code____0, ~Instruction[0], ~Instruction[2], ~Instruction[3], ~Instruction[4], ~Instruction[5]);  // AND_Gate
  and and_3 (op_code____1, Instruction[26], Instruction[28], Instruction[29], Instruction[30], Instruction[31]);
  and and_4 (op_code____0, ~Instruction[26], ~Instruction[27], ~Instruction[28], ~Instruction[30], ~Instruction[30], ~Instruction[31]);  // AND_Gate
  and and_5 (branch_t, ~Instruction[29], ~Instruction[30], ~Instruction[31], ~op_code____0);  // AND_Gate
  and and_6 (pop_push, ~Instruction[26], ~Instruction[28], Instruction[29], Instruction[30], Instruction[31]);  // AND_Gate
  and and_7 (func_code____011, Instruction[3], Instruction[4], ~Instruction[5]);  // AND_Gate
  or or_1 (lw_sw, lw, sw);
  and and_8 (halt, op_code____1, func_code____1);
  and and_9 (nop, op_code____0, func_code____0);
  and and_10 (ai, opp_aritmetica, inmediate);
  and and_11 (add_i, ~Instruction[26], ~Instruction[27], ~Instruction[28], ai);  // AND_Gate
  and and_12 (slt_i, ~Instruction[26], Instruction[27], ~Instruction[28], ai);  // AND_Gate
  and and_13 (sltu_i, Instruction[26], Instruction[27], ~Instruction[28], ai);  // AND_Gate
  and and_14 (and_i, ~Instruction[26], ~Instruction[27], Instruction[28], ai);  // AND_Gate
  and and_15 (or_i, Instruction[26], ~Instruction[27], Instruction[28], ai);  // AND_Gate
  and and_16 (xor_i, ~Instruction[26], Instruction[27], Instruction[28], ai);  // AND_Gate
  and and_17 (and_17_out, Instruction[29], ~Instruction[30], ~Instruction[31]);  // AND_Gate
  and and_18 (and_18_out, Instruction[29], ~Instruction[30], ~Instruction[31]);  // AND_Gate
  or or_2 (RF_zero, blez, bgtz, bltz);
  and and_19 (and_19_out, opp_aritmetica, ~inmediate);  // AND_Gate
  and and_20 (and_20_out, ~load_Rd, ~inmediate);  // AND_Gate
  Priority_Encoder #(.select(2)) priority_encoder_1 (
    .in0(1'b1), .in1(mfhi), .in2(mflo), .in3(or_3_out), .out(data_to_RF));  // open: gs, en_out, en_in
  or or_3 (or_3_out, pop, lw);
  and and_21 (tty, op_code____1, ~halt, Instruction[0]);  // AND_Gate
  and and_22 (rnd, op_code____1, ~halt, Instruction[1]);  // AND_Gate
  and and_23 (kbd, op_code____1, ~halt, Instruction[2]);  // AND_Gate
  or or_4 (opp_aritmetica, and_17_out, and_24_out);
  and and_24 (and_24_out, op_code____0, ~nop, ~mfhi, ~mflo, ~jr, ~func_code____011);  // AND_Gate
  or or_5 (inmediate, and_18_out, lw, sw);
  or or_6 (load_Rd, and_19_out, rnd, mflo, pop, mfhi, kbd);
  or or_7 (load_zero, and_20_out, sw);
  or or_8 (logic_i, and_i, or_i, xor_i);
  and and_25 (mfhi, op_code____0, ~Instruction[0], ~Instruction[1], ~Instruction[2], ~Instruction[3], Instruction[4], ~Instruction[5]);  // AND_Gate
  and and_26 (mflo, op_code____0, ~Instruction[0], Instruction[1], ~Instruction[2], ~Instruction[3], Instruction[4], ~Instruction[5]);  // AND_Gate
  and and_27 (lw, Instruction[26], Instruction[27], ~Instruction[28], ~Instruction[29], ~Instruction[30], Instruction[31]);  // AND_Gate
  or or_9 (or_9_out, add, add_i, lw_sw);
  or or_10 (or_10_out, branch_t, sub);
  or or_11 (or_11_out, slt, slt_i);
  or or_12 (or_12_out, slt_u, sltu_i);
  or or_13 (or_13_out, \and , and_i);
  or or_14 (or_14_out, \or , or_i);
  or or_15 (or_15_out, \xor , xor_i);
  Priority_Encoder #(.select(4)) priority_encoder_2 (
    .in0(or_9_out), .in1(or_10_out), .in2(mul), .in3(mul_u), .in4(div), .in5(div_u), .in6(or_11_out),
    .in7(or_12_out), .in8(or_13_out), .in9(or_14_out), .in10(\nor ), .in11(or_15_out), .out(alu_operator));  // open: in12, in13, in14, in15, gs, en_out, en_in
  and and_28 (sw, Instruction[26], Instruction[27], ~Instruction[28], Instruction[29], ~Instruction[30], Instruction[31]);  // AND_Gate
  and and_29 (and_29_out, op_code____0, func_code____011);
  or or_16 (a, and_29_out, and_30_out);
  and and_30 (and_30_out, opp_aritmetica, op_code____0);
  or or_17 (mul_div, mul, mul_u, div, div_u);
  and and_31 (j, ~Instruction[26], Instruction[27], ~Instruction[28], ~Instruction[29], ~Instruction[30], ~Instruction[31]);  // AND_Gate
  and and_32 (jr, op_code____0, ~Instruction[0], ~Instruction[1], ~Instruction[2], Instruction[3], ~Instruction[4], ~Instruction[5]);  // AND_Gate
  and and_33 (add, a, ~Instruction[0], ~Instruction[1], ~Instruction[2], ~Instruction[3], ~Instruction[4], Instruction[5]);  // AND_Gate
  and and_34 (sub, a, ~Instruction[0], Instruction[1], ~Instruction[2], ~Instruction[3], ~Instruction[4], Instruction[5]);  // AND_Gate
  and and_35 (mul, a, ~Instruction[0], ~Instruction[1], ~Instruction[2], Instruction[3], Instruction[4], ~Instruction[5]);  // AND_Gate
  and and_36 (mul_u, a, Instruction[0], ~Instruction[1], ~Instruction[2], Instruction[3], Instruction[4], ~Instruction[5]);  // AND_Gate
  and and_37 (\and , a, ~Instruction[0], ~Instruction[1], Instruction[2], ~Instruction[3], ~Instruction[4], Instruction[5]);  // AND_Gate
  and and_38 (\or , a, Instruction[0], ~Instruction[1], Instruction[2], ~Instruction[3], ~Instruction[4], Instruction[5]);  // AND_Gate
  and and_39 (pop, pop_push, func_code____0);
  and and_40 (be, ~Instruction[26], ~Instruction[27], Instruction[28], branch_t);  // AND_Gate
  and and_41 (bne, Instruction[26], ~Instruction[27], Instruction[28], branch_t);  // AND_Gate
  assign Aritmetic_Op[31:16] = {{15{1'b0}}, Instruction[15]};  // Bit_Extender bit_extender_1
  assign Branch[31:18] = {{13{1'b0}}, Instruction[15]};  // Bit_Extender bit_extender_2
  and and_42 (blez, ~Instruction[26], Instruction[27], Instruction[28], branch_t);  // AND_Gate
  and and_43 (div, a, ~Instruction[0], Instruction[1], ~Instruction[2], Instruction[3], Instruction[4], ~Instruction[5]);  // AND_Gate
  and and_44 (div_u, a, Instruction[0], Instruction[1], ~Instruction[2], Instruction[3], Instruction[4], ~Instruction[5]);  // AND_Gate
  and and_45 (slt, a, ~Instruction[0], Instruction[1], ~Instruction[2], Instruction[3], ~Instruction[4], Instruction[5]);  // AND_Gate
  and and_46 (slt_u, a, Instruction[0], Instruction[1], ~Instruction[2], Instruction[3], ~Instruction[4], Instruction[5]);  // AND_Gate
  and and_47 (\nor , a, Instruction[0], Instruction[1], Instruction[2], ~Instruction[3], ~Instruction[4], Instruction[5]);  // AND_Gate
  and and_48 (\xor , a, ~Instruction[0], ~Instruction[1], ~Instruction[2], Instruction[3], ~Instruction[4], Instruction[5]);  // AND_Gate
  and and_49 (bgtz, Instruction[26], Instruction[27], Instruction[28], branch_t);
  and and_50 (bltz, Instruction[26], ~Instruction[27], ~Instruction[28], branch_t);  // AND_Gate
  and and_51 (push, pop_push, Instruction[0], ~Instruction[1], ~Instruction[2], ~Instruction[3], ~Instruction[4], ~Instruction[5]);  // AND_Gate

  assign Aritmetic_Op[15:0] = Instruction[15:0];
  assign Branch[17:0] = {Instruction[15:0], 2'b00};
  assign destino = {Instruction[25:0], 2'b00};
  assign Logic_Op = {{16{1'b0}}, Instruction[15:0]};
  assign Rd = Instruction[15:11];
  assign Rs = Instruction[25:21];
  assign Rt = Instruction[20:16];

  // Other names for the same wires on the sheet: alu_operador[3:0] = alu_operator; constant[15:0] = Instruction[15:0];
  //   destiny[25:0] = Instruction[25:0]; func_code[5:0] = Instruction[5:0]; op_code[5:0] = Instruction[31:26]

  // Notes on the sheet:
  //   INPUT
  //   DECODER
  //   GENERAL
  //   INMEDIATE
  //   MFHI && MFLO
  //   LOAD/STORE WORD
  //   JUMP
  //   ARITMETIC
  //   INSTRUCTION DECODER
  //   OUTPUTS
  //   BRANCH
  //   POP/PUSH
endmodule

module Datapath (
  input  [31:0] Data,
  input  clr_I,
  input  en,
  input  Pop_load,
  input  exc_I_2,
  input  Push_load,
  input  load_I,
  input  clk,
  input  exc_I,
  input  clr,
  input  [6:0] kbd_data,
  input  kbd_aviable
);

  wire [31:0] bit_extender_1_out, kbd_data_t;

  assign bit_extender_1_out = {{25{1'b0}}, kbd_data};  // Bit_Extender bit_extender_1
  Multiplexer #(.width(32), .enable("false")) multiplexer_1 (
    .in0({32{1'b1}}), .in1(bit_extender_1_out), .out(kbd_data_t), .sel(kbd_aviable));
  Instruction_Decoder instruction_decoder_1 ();  // open: Instruction, Logic_Op, Aritmetic_Op, Branch, nop, tty, mfhi, mflo, be, halt, rnd, kbd, j, jr, destino, Rs, pop, push, logic_i, Rt, lw, sw, Rd, mul_div, alu_operator, bne, load_zero, blez, data_to_RF, RF_zero, pop_push, bgtz, load_Rd, lw_sw, inmediate, bltz
endmodule

module Repetidor (
  input  Signal,
  output [15:0] _16,
  output [13:0] _14
);


  assign _14 = {14{Signal}};
  assign _16 = {16{Signal}};
endmodule

module Memory_Manager (
  input  Start,
  input  CS,
  input  CLK,
  input  CLR,
  input  R_W_Time_Selector,
  input  [3:0] Read_Time,
  input  [3:0] Write_Time,
  input  [31:0] Address_In,
  input  [31:0] Register,
  input  [31:0] RAM_out_0,
  input  [31:0] RAM_out_1,
  input  [31:0] RAM_out_2,
  input  [31:0] RAM_out_3,
  output [31:0] RAM_in_0,
  output [31:0] RAM_in_1,
  output [31:0] RAM_in_2,
  output [31:0] RAM_in_3,
  output [31:0] Out,
  output R_W,
  output [3:0] RAM_massk,
  output [15:0] Address
);

  wire [31:0] demultiplexer_1_out1;

  Decoder #(.select(2), .enable("false")) decoder_1 (
    .out0(RAM_massk[0]), .out1(RAM_massk[1]), .out2(RAM_massk[2]), .out3(RAM_massk[3]), .sel(Address_In[3:2]));
  Multiplexer #(.select(2), .width(32), .enable("false")) multiplexer_1 (
    .in0(RAM_out_0), .in1(RAM_out_1), .in2(RAM_out_2), .in3(RAM_out_3),
    .out({Out[7:0], Out[15:8], Out[23:16], Out[31:24]}), .sel(Address_In[3:2]));
  Demultiplexer #(.width(32), .enable("false")) demultiplexer_1 (
    .out1(demultiplexer_1_out1), .in({Register[7:0], Register[15:8], Register[23:16], Register[31:24]}),
    .sel(R_W_Time_Selector));  // open: out0
  Demultiplexer #(.select(2), .width(32), .enable("false")) demultiplexer_2 (
    .out0(RAM_in_0), .out1(RAM_in_1), .out2(RAM_in_2), .out3(RAM_in_3), .in(demultiplexer_1_out1),
    .sel(Address_In[3:2]));

  assign Address = Address_In[19:4];
  assign R_W = R_W_Time_Selector;

  // Other names for the same wires on the sheet: block[1:0] = Address_In[3:2]; ADDR[15:0] = Address_In[19:4];
  //   R_T[3:0] = Read_Time; R_W_TS = R_W_Time_Selector; RAM_input_1[31:0] = RAM_in_1; RAM_input_2[31:0] = RAM_in_2;
  //   RAM_input_3[31:0] = RAM_in_3; RAM_inputt_0[31:0] = RAM_in_0; RAM_mask[3:0] = RAM_massk; W_T[3:0] = Write_Time

  // Notes on the sheet:
  //   input
  //   output
endmodule

module Cronometer (
  input  Start,
  input  CLK,
  input  [3:0] Time,
  input  Clear,
  output Ready
);

  Counter #(.width(4), .max('hf)) counter_1 (
    .load(1'b1), .D(Time), .count(Start), .carry(Ready), .clk(CLK), .clr(Clear));  // open: Q
endmodule

module Control_Unit (
  input  in_1,
  input  in_2,
  input  in_3,
  input  in_4,
  input  in_5,
  input  in_6,
  input  [2:0] in_7,
  input  [1:0] Data_To_Memory,
  input  [1:0] Adress_To_Memory,
  input  Enable_Datapath_Branch,
  output CS,
  output R_W,
  output Load_Instruction,
  output EN_Datapath
);

  wire ALU_Add, CS_Instruction, CS_Pop, demultiplexer_1_out0, demultiplexer_1_out1, demultiplexer_2_out0,
       demultiplexer_3_out1, demultiplexer_4_out0, demultiplexer_5_out0, demultiplexer_6_out0,
       demultiplexer_6_out1, demultiplexer_7_out0, demultiplexer_7_out1, Enable_Datapath_Estrict,
       Enable_Datapath_LW, Enable_Datapath_LW2, Enable_Datapath_Pop, Enable_Datapath_Push,
       Enable_Datapath_SW, IDLE_q, or_1_out, or_2_out, or_6_out, or_9_out, or_10_out, or_11_out, or_12_out,
       or_13_out, Regiester_Add, SP_Add;

  or or_1 (or_1_out, in_1, ~in_5);  // OR_Gate
  D_Flip_Flop IDLE (.clk(in_2), .D(demultiplexer_1_out0), .Q(IDLE_q), .preset(or_1_out));  // open: Qn, en, reset
  or or_2 (or_2_out, IDLE_q, Enable_Datapath_Branch);
  or or_3 (CS, CS_Instruction, CS_Pop, R_W, R_W);
  or or_4 (SP_Add, CS_Pop, R_W);
  or or_5 (Regiester_Add, R_W, R_W);
  Demultiplexer #(.enable("false")) demultiplexer_1 (
    .out0(demultiplexer_1_out0), .out1(demultiplexer_1_out1), .in(or_2_out), .sel(in_5));
  or or_6 (or_6_out, demultiplexer_2_out0, demultiplexer_1_out1);
  or or_7 (ALU_Add, R_W, R_W);
  Demultiplexer #(.enable("false")) demultiplexer_2 (
    .out0(demultiplexer_2_out0), .out1(Load_Instruction), .in(CS_Instruction), .sel(in_6));
  D_Flip_Flop u_Load_Instruction (.clk(in_2), .D(or_6_out), .Q(CS_Instruction), .reset(in_1));  // open: Qn, preset, en
  or or_8 (EN_Datapath, Enable_Datapath_Pop, Enable_Datapath_LW2, Enable_Datapath_LW, Enable_Datapath_Estrict, Enable_Datapath_Push);
  Demultiplexer #(.select(3), .enable("false")) demultiplexer_3 (
    .out0(Enable_Datapath_Estrict), .out1(demultiplexer_3_out1), .out2(Enable_Datapath_Push),
    .out3(Enable_Datapath_LW), .out4(Enable_Datapath_SW), .in(Load_Instruction), .sel(in_7));  // open: out5, out6, out7
  Priority_Encoder #(.select(2)) priority_encoder_1 (
    .in0(SP_Add), .in1(CS_Instruction), .in2(ALU_Add), .in3(Regiester_Add), .out(Adress_To_Memory));  // open: gs, en_out, en_in
  D_Flip_Flop #(.trigger("falling")) Read (.clk(in_2), .D(or_9_out), .Q(CS_Pop), .reset(in_1));  // open: Qn, preset, en
  or or_9 (or_9_out, demultiplexer_4_out0, demultiplexer_3_out1);
  Demultiplexer #(.enable("false")) demultiplexer_4 (
    .out0(demultiplexer_4_out0), .out1(Enable_Datapath_Pop), .in(CS_Pop), .sel(in_6));
  or or_10 (or_10_out, demultiplexer_7_out0, Enable_Datapath_Push);
  or or_11 (or_11_out, demultiplexer_5_out0, Enable_Datapath_LW);
  or or_12 (or_12_out, demultiplexer_6_out0, Enable_Datapath_SW);
  D_Flip_Flop #(.trigger("falling")) Write (.clk(in_2), .D(or_10_out), .Q(R_W), .reset(in_1));  // open: Qn, preset, en
  D_Flip_Flop #(.trigger("falling")) Write_2 (
    .clk(in_2), .D(or_11_out), .Q(R_W), .reset(in_1));  // open: Qn, preset, en
  D_Flip_Flop #(.trigger("falling")) Write_3 (
    .clk(in_2), .D(or_12_out), .Q(R_W), .reset(in_1));  // open: Qn, preset, en
  Demultiplexer #(.enable("false")) demultiplexer_5 (
    .out0(demultiplexer_5_out0), .out1(Enable_Datapath_LW2), .in(R_W), .sel(in_6));
  Demultiplexer #(.enable("false")) demultiplexer_6 (
    .out0(demultiplexer_6_out0), .out1(demultiplexer_6_out1), .in(R_W), .sel(in_6));
  Demultiplexer #(.enable("false")) demultiplexer_7 (
    .out0(demultiplexer_7_out0), .out1(demultiplexer_7_out1), .in(R_W), .sel(in_6));
  D_Flip_Flop #(.trigger("falling")) End (
    .clk(in_2), .D(or_13_out), .Q(Enable_Datapath_Branch), .reset(in_1));  // open: Qn, preset, en
  or or_13 (or_13_out, Enable_Datapath_Pop, demultiplexer_7_out1, Enable_Datapath_LW2, Enable_Datapath_Estrict, demultiplexer_6_out1);

  // Other names for the same wires on the sheet: Clk = in_2; Enable_Datapath = EN_Datapath; Instruction[2:0] = in_7;
  //   L_S = in_4; Mem_End = in_6; P_pop = in_3; PC_Add = CS_Instruction; End = Enable_Datapath_Branch;
  //   PC_Update = Enable_Datapath_Branch; Reset = in_1; SP_Add_Pop = CS_Pop; ALU_Add_LW = R_W; ALU_Add_SW = R_W;
  //   CS_LW = R_W; CS_Push = R_W; Register_Data_Push = R_W; Register_Data_SW = R_W; SP_Add_Push = R_W; start = in_5

  // Notes on the sheet:
  //   Ouput Data
  //   Input Data
  //   Managing Repetitions of Signals
  //   POP
  //   PUSH
  //   LW
  //   SW
  //   Estrict Datapath Operation
endmodule
