// Logisim project Ray-Implementations.circ as structural Verilog
module ALU (
  input  [31:0] A,
  input  [31:0] B,
  input  [3:0] S,
  output [31:0] R,
  output [31:0] hi,
  output zero,
  output [31:0] lo,
  output neg
);

  wire comparator_2_lt, comparator_3_lt, HL0;
  wire [31:0] ADD, AND, DIVS_HI, DIVS_LO, DIVU_HI, DIVU_LO, MULT_HI, MULT_LO, MULU_HI, MULU_LO, NOR, OR, SLT,
       SLTU, SUB, XOR;

  // Probe on A
  Adder #(.width(32)) adder_1 (.a(A), .b(B), .out(ADD));  // open: cin, cout
  Subtractor #(.width(32)) subtractor_1 (.a(A), .b(B), .out(SUB));  // open: bin, bout
  assign OR = A | B;  // OR_Gate or_1, 32 bits wide
  assign AND = A & B;  // AND_Gate and_1, 32 bits wide
  Multiplexer #(.select(2), .width(32), .enable("false")) multiplexer_1 (
    .in0(MULT_HI), .in1(MULU_HI), .in2(DIVS_HI), .in3(DIVU_HI), .out(hi), .sel({HL0, S[0]}));
  or or_2 (HL0, S[2], S[3]);
  // Probe on B
  Multiplier #(.width(32)) multiplier_1 (.a(A), .b(B), .out(MULT_LO), .cout(MULT_HI));  // open: cin
  Divider #(.width(32)) divider_1 (.a(A), .b(B), .out(DIVU_LO), .rem(DIVU_HI));  // open: upper
  assign NOR = ~(A | B);  // NOR_Gate nor_1, 32 bits wide
  assign XOR = A ^ B;  // XOR_Gate xor_1, 32 bits wide
  // Probe on lo
  Comparator #(.width(32)) comparator_1 (.a(lo), .b({32{1'b0}}), .eq(zero), .lt(neg));  // open: gt
  DivS divs_1 (.A(A), .B(B), .LowOutput(DIVS_LO), .HighOutput(DIVS_HI));
  MultU multu_1 (.in_1(A), .in_2(B), .low(MULU_LO), .hi(MULU_HI));
  Multiplexer #(.width(32), .enable("false")) multiplexer_2 (
    .in0({32{1'b0}}), .in1(32'h1), .out(SLT), .sel(comparator_2_lt));
  Comparator #(.width(32)) comparator_2 (.a(A), .b(B), .lt(comparator_2_lt));  // open: gt, eq
  Multiplexer #(.width(32), .enable("false")) multiplexer_3 (
    .in0({32{1'b0}}), .in1(32'h1), .out(SLTU), .sel(comparator_3_lt));
  Comparator #(.width(32), .mode("unsigned")) comparator_3 (.a(A), .b(B), .lt(comparator_3_lt));  // open: gt, eq
  Multiplexer #(.select(4), .width(32), .enable("false")) multiplexer_4 (
    .in0(ADD), .in1(SUB), .in2(MULT_LO), .in3(MULU_LO), .in4(DIVS_LO), .in5(DIVU_LO), .in6(SLT), .in7(SLTU),
    .in8(AND), .in9(OR), .in10(NOR), .in11(XOR), .out(lo), .sel(S));  // open: in12, in13, in14, in15
  // Probe on hi

  assign R = lo;

  // Other names for the same wires on the sheet: RESULT[31:0] = lo; HL = S[0]; SELECT[3:0] = S

  // Notes on the sheet:
  //   ARITMÉTICA
  //   LÓGICA
  //   INPUTS
  //   MULT
  //   DIVU
  //   HILO SELECTOR
  //   COMPARACIÓN
  //   0000
  //   0001
  //   0010
  //   0011
  //   0100
  //   0101
  //   0110
  //   0111
  //   1000
  //   1001
  //   1010
  //   1011
  //   OUTPUTS
  //   OPERATION SELECTOR
endmodule

module DivS (
  input  [31:0] A,
  input  [31:0] B,
  output [31:0] LowOutput,
  output [31:0] HighOutput
);

  wire xor_1_out;
  wire [31:0] divider_1_out, multiplexer_1_out, multiplexer_2_out, negator_1_out, negator_2_out,
       negator_3_out;

  Negator #(.width(32)) negator_1 (.in(A), .out(negator_1_out));
  Negator #(.width(32)) negator_2 (.in(B), .out(negator_2_out));
  Multiplexer #(.width(32), .enable("false")) multiplexer_1 (
    .in0(A), .in1(negator_1_out), .out(multiplexer_1_out), .sel(A[31]));
  Multiplexer #(.width(32), .enable("false")) multiplexer_2 (
    .in0(B), .in1(negator_2_out), .out(multiplexer_2_out), .sel(B[31]));
  Divider #(.width(32)) divider_1 (
    .a(multiplexer_1_out), .b(multiplexer_2_out), .out(divider_1_out), .rem(HighOutput));  // open: upper
  Negator #(.width(32)) negator_3 (.in(divider_1_out), .out(negator_3_out));
  xor xor_1 (xor_1_out, A[31], B[31]);
  // Probe on LowOutput
  Multiplexer #(.width(32), .enable("false")) multiplexer_3 (
    .in0(divider_1_out), .in1(negator_3_out), .out(LowOutput), .sel(xor_1_out));
  // Probe on HighOutput

  // Notes on the sheet:
  //   SIGNED DIV
endmodule

module MultU (
  input  [31:0] in_1,
  input  [31:0] in_2,
  output [31:0] low,
  output [31:0] hi
);

  wire C_S_low1, C_S_low2, C_S_low3, carry, carry2, S3;
  wire [31:0] A_S2, AL, AR, ARxBR_hi, ARxBR_low, B_S1, bit_extender_1_out, bit_extender_2_out,
       bit_extender_3_out, bit_extender_4_out, BL, BR, hi1, hi2, low1, low2, S_hi1, S_hi2, S_low1, S_low2;

  shift shift_1 (.in_1(1'b0), .in_2(ARxBR_low), .Output0(carry), .Output(low1));
  shift shift_2 (.in_1(1'b0), .in_2(low1), .Output0(carry2), .Output(low2));
  shift shift_3 (.in_1(carry), .in_2(ARxBR_hi), .Output(hi1));  // open: Output0
  shift shift_4 (.in_1(carry2), .in_2(hi1), .Output(hi2));  // open: Output0
  Shifter #(.width(32), .shift("lr")) shifter_1 (.in(in_1), .\dist (5'b00001), .out(AR));
  Shifter #(.width(32), .shift("lr")) shifter_2 (.in(in_2), .\dist (5'b00001), .out(BR));
  Multiplier #(.width(32)) multiplier_1 (.a(AR), .b(BR), .out(ARxBR_low), .cout(ARxBR_hi));  // open: cin
  Adder #(.width(32)) adder_1 (.a(A_S2), .b(low2), .out(S_low1), .cout(C_S_low1));  // open: cin
  Adder #(.width(32)) adder_2 (.a(B_S1), .b(S_low1), .out(S_low2), .cout(C_S_low2));  // open: cin
  assign bit_extender_1_out = {{31{1'b0}}, S3};  // Bit_Extender bit_extender_1
  Adder #(.width(32)) adder_3 (.a(bit_extender_1_out), .b(S_low2), .out(low), .cout(C_S_low3));  // open: cin
  Shifter #(.width(32)) shifter_3 (.in(AR), .\dist (5'b00001), .out(AL));
  Shifter #(.width(32)) shifter_4 (.in(BR), .\dist (5'b00001), .out(BL));
  assign bit_extender_2_out = {{31{1'b0}}, C_S_low1};  // Bit_Extender bit_extender_2
  assign bit_extender_3_out = {{31{1'b0}}, C_S_low2};  // Bit_Extender bit_extender_3
  assign bit_extender_4_out = {{31{1'b0}}, C_S_low3};  // Bit_Extender bit_extender_4
  Multiplexer #(.width(32), .enable("false")) multiplexer_1 (.in0({32{1'b0}}), .in1(AL), .out(A_S2), .sel(in_2[0]));
  Multiplexer #(.width(32), .enable("false")) multiplexer_2 (.in0({32{1'b0}}), .in1(BL), .out(B_S1), .sel(in_1[0]));
  Adder #(.width(32)) adder_4 (.a(bit_extender_2_out), .b(hi2), .out(S_hi1));  // open: cin, cout
  Adder #(.width(32)) adder_5 (.a(bit_extender_3_out), .b(S_hi1), .out(S_hi2));  // open: cin, cout
  Adder #(.width(32)) adder_6 (.a(bit_extender_4_out), .b(S_hi2), .out(hi));  // open: cin, cout
  and and_1 (S3, in_1[0], in_2[0]);

  // Other names for the same wires on the sheet: A[31:0] = in_1; S1 = in_1[0]; B[31:0] = in_2; S2 = in_2[0];
  //   S_hi[31:0] = hi; S_low[31:0] = low
endmodule

module shift (
  input  in_1,
  input  [31:0] in_2,
  output Output0,
  output [31:0] Output
);


  assign Output = {in_2[30:0], in_1};
  assign Output0 = in_2[31];
endmodule

module Branch_Control (
  input  J,
  input  BEQ,
  input  [31:0] Rs,
  input  JR,
  input  BNE,
  input  ZERO,
  input  BLEZ,
  input  [31:0] PC,
  input  NEG,
  input  BGTZ,
  input  BLTZ,
  input  [31:0] in_12,
  input  [27:0] in_13,
  output [31:0] Result
);

  wire and_5_out, beq_t, bgtz_t, blez_t, bltz_t, bne_t, or_1_out;
  wire [1:0] SEL;
  wire [31:0] PC_4, PC_4_REL, Rs_t;

  and and_1 (beq_t, BEQ, ZERO);
  and and_2 (bne_t, BNE, ~ZERO);  // AND_Gate
  and and_3 (blez_t, BLEZ, NEG);
  or or_1 (or_1_out, beq_t, bne_t, blez_t, bgtz_t, bltz_t);
  and and_4 (bgtz_t, BGTZ, ~NEG);  // AND_Gate
  and and_5 (and_5_out, ~ZERO, NEG);  // AND_Gate
  Priority_Encoder #(.select(2)) priority_encoder_1 (
    .in0(1'b1), .in1(or_1_out), .in2(J), .in3(JR), .out(SEL));  // open: gs, en_out, en_in
  and and_6 (bltz_t, and_5_out, BLTZ);
  Adder #(.width(32)) adder_1 (.a(PC), .b(32'h4), .out(PC_4));  // open: cin, cout
  Adder #(.width(32)) adder_2 (.a(PC_4), .b(in_12), .out(PC_4_REL));  // open: cin, cout
  Multiplexer #(.select(2), .width(32), .enable("false")) multiplexer_1 (
    .in0(PC_4), .in1(PC_4_REL), .in2({PC[31:28], in_13}), .in3(Rs_t), .out(Result), .sel(SEL));

  // Other names for the same wires on the sheet: DESTINY_JUMP[31:0] = {PC[31:28], in_13}; RELATIVE[31:0] = in_12

  // Notes on the sheet:
  //   PC SELECTOR
  //   INPUTS
  //   PC SELECTION
  //   BRANCH CONTROL
endmodule
