// Logisim project s-mips.circ as structural Verilog: 15 circuits, main circuit S-MIPS Board
module S_MIPS_Board (
  input  DESHABILITAR_DISPATCHER,
  output halt
);

  wire button_1_out, CLK, CS, d_ff_1_q, LCLR, LoadRAM, LoadRAMOn, LW, R_R_W, R_W, ram_dispatcher_1_finished,
       RCS, Reset_out, RST, TTY_EN;
  wire [2:0] KDB;
  wire [3:0] LMask, Mask, ram_1_read_time, ram_1_write_time, RMask;
  wire [6:0] KDB_DATA, TTY_DATA;
  wire [15:0] Addr, LAddr, RAddr;
  wire [31:0] I0, I1, I2, I3, LData, ram_1_data_out_0, ram_1_data_out_1, ram_1_data_out_2, ram_1_data_out_3,
       RI0, RI1, RI2, RI3;

  TTY #(.rows(25), .cols(80)) tty_1 (.data(TTY_DATA), .clk(CLK), .we(TTY_EN), .clr(RST));
  not not_1 (LoadRAMOn, ram_dispatcher_1_finished);
  RAM_Dispatcher ram_dispatcher_1 (
    .WriteTime(ram_1_write_time), .Clock(CLK), .Data(LData), .Address(LAddr), .Mask(LMask),
    .Finished(ram_dispatcher_1_finished), .Write(LW), .CLR(LCLR));
  Keyboard #(.buflen(64)) keyboard_1 (.clk(CLK), .re(KDB[0]), .clr(KDB[1]), .avail(KDB[2]), .data(KDB_DATA));
  RAM ram_1 (
    .Address(RAddr), .Data_Out_0(ram_1_data_out_0), .Data_Out_1(ram_1_data_out_1),
    .Data_Out_2(ram_1_data_out_2), .Data_Out_3(ram_1_data_out_3), .Data_In_0(RI0), .Data_In_1(RI1),
    .Data_In_2(RI2), .Data_In_3(RI3), .Mask(RMask), .nRead_Write(R_R_W), .Chip_Select(RCS),
    .Read_Time(ram_1_read_time), .Reset(button_1_out), .Write_Time(ram_1_write_time));
  Button button_1 (.out(button_1_out));
  D_Flip_Flop d_ff_1 (.clk(CLK), .D(1'b1), .Q(d_ff_1_q), .reset(Reset_out));  // open: Qn, preset, en
  Button Reset (.out(Reset_out));
  S_MIPS s_mips_1 (
    .Kbd_Enable(KDB[0]), .Address(Addr), .Kbd_Clear(KDB[1]), .Kbd_Available(KDB[2]), .RAM_In_0(I0),
    .Kbd_ASCII_Data(KDB_DATA), .RAM_In_1(I1), .TTY_Enable(TTY_EN), .RAM_In_2(I2), .RAM_In_3(I3),
    .TTY_ASCII_Data(TTY_DATA), .Reset(RST), .RAM_Out_0(ram_1_data_out_0), .Clock(CLK),
    .RAM_Out_1(ram_1_data_out_1), .Stop(halt), .RAM_Out_2(ram_1_data_out_2), .RAM_Out_3(ram_1_data_out_3),
    .Mask(Mask), .Read_Time(ram_1_read_time), .Write_Time(ram_1_write_time), .nRead_Write(R_W),
    .Chip_Select(CS));
  D_Flip_Flop d_ff_2 (.clk(CLK), .D(d_ff_1_q), .Qn(LCLR), .reset(Reset_out));  // open: Q, preset, en
  or or_1 (RST, LCLR, LoadRAM);
  Clock clock_1 (.out(CLK));
  Multiplexer #(.width(32), .enable("false")) multiplexer_1 (.in0(I0), .in1(LData), .out(RI0), .sel(LoadRAM));
  Multiplexer #(.width(32), .enable("false")) multiplexer_2 (.in0(I1), .in1(LData), .out(RI1), .sel(LoadRAM));
  Multiplexer #(.width(32), .enable("false")) multiplexer_3 (.in0(I2), .in1(LData), .out(RI2), .sel(LoadRAM));
  Multiplexer #(.width(32), .enable("false")) multiplexer_4 (.in0(I3), .in1(LData), .out(RI3), .sel(LoadRAM));
  and and_1 (LoadRAM, ~DESHABILITAR_DISPATCHER, LoadRAMOn);  // AND_Gate
  Multiplexer #(.width(16), .enable("false")) multiplexer_5 (.in0(Addr), .in1(LAddr), .out(RAddr), .sel(LoadRAM));
  Multiplexer #(.width(4), .enable("false")) multiplexer_6 (.in0(Mask), .in1(LMask), .out(RMask), .sel(LoadRAM));
  Multiplexer #(.enable("false")) multiplexer_7 (.in0(CS), .in1(LW), .out(RCS), .sel(LoadRAM));
  Multiplexer #(.enable("false")) multiplexer_8 (.in0(R_W), .in1(LW), .out(R_R_W), .sel(LoadRAM));

  // Notes on the sheet:
  //   NO MODIFICAR
  //   Keyboard
endmodule

module RAM (
  input  [15:0] Address,
  input  [31:0] Data_In_0,
  input  [31:0] Data_In_1,
  input  [31:0] Data_In_2,
  input  [31:0] Data_In_3,
  input  [3:0] Mask,
  input  nRead_Write,
  input  Chip_Select,
  input  Reset,
  output [31:0] Data_Out_0,
  output [31:0] Data_Out_1,
  output [31:0] Data_Out_2,
  output [31:0] Data_Out_3,
  output [3:0] Read_Time,
  output [3:0] Write_Time
);

  wire and_2_out, and_3_out, and_4_out, and_5_out, and_6_out, and_7_out, and_8_out, and_9_out, Changed, CLK,
       comparator_2_eq, comparator_3_eq, comparator_4_eq, comparator_5_eq, comparator_6_eq, Count,
       demultiplexer_3_out0, Idle, Idle_q, Load, Load0, Load1, nand_1_out, or_1_out, or_2_out, or_3_out,
       or_4_out, or_5_out, or_6_out, or_7_out, or_8_out, or_9_out, or_10_out, Proc_q, Update_Mem, Zero_Time;
  wire [3:0] counter_1_q, multiplexer_1_out, subtractor_1_out;
  wire [31:0] register_1_q, register_2_q, register_3_q, register_4_q, register_5_q;

  // Probe on 4'b0011
  // Probe on 4'b0010
  Multiplexer #(.width(4), .enable("false")) multiplexer_1 (
    .in0(4'b0011), .in1(4'b0010), .out(multiplexer_1_out), .sel(nRead_Write));
  or or_1 (or_1_out, Idle, Update_Mem);
  or or_2 (or_2_out, ~Chip_Select, Reset);  // OR_Gate
  Subtractor #(.width(4)) subtractor_1 (.a(multiplexer_1_out), .b(4'b0010), .out(subtractor_1_out));  // open: bin, bout
  Demultiplexer #(.enable("false")) demultiplexer_1 (.out0(Idle), .out1(Load0), .in(Idle_q), .sel(Changed));
  D_Flip_Flop u_Idle (.clk(CLK), .D(or_1_out), .Q(Idle_q), .preset(or_2_out));  // open: Qn, en, reset
  // Probe on counter_1_q
  Counter #(.width(4), .max('hf)) counter_1 (
    .load(Load), .D(subtractor_1_out), .count(Count), .Q(counter_1_q), .clk(CLK), .clr(or_3_out));  // open: carry
  or or_3 (or_3_out, ~Chip_Select, Reset);  // OR_Gate
  Comparator #(.width(4), .mode("unsigned")) comparator_1 (
    .a(4'b0000), .b(counter_1_q), .eq(Zero_Time));  // open: gt, lt
  or or_4 (or_4_out, Count, Load0, Load1);
  Register #(.width(32)) register_1 (.D(Data_In_0), .en(Chip_Select), .Q(register_1_q), .clk(CLK), .clr(or_5_out));
  or or_5 (or_5_out, ~Chip_Select, Reset);  // OR_Gate
  Register #(.width(32)) register_2 (.D(Data_In_1), .en(Chip_Select), .Q(register_2_q), .clk(CLK), .clr(or_6_out));
  or or_6 (or_6_out, ~Chip_Select, Reset);  // OR_Gate
  Register #(.width(32)) register_3 (.D(Data_In_2), .en(Chip_Select), .Q(register_3_q), .clk(CLK), .clr(or_7_out));
  or or_7 (or_7_out, ~Chip_Select, Reset);  // OR_Gate
  Register #(.width(32)) register_4 (.D(Data_In_3), .en(Chip_Select), .Q(register_4_q), .clk(CLK), .clr(or_8_out));
  or or_8 (or_8_out, ~Chip_Select, Reset);  // OR_Gate
  Register #(.width(32)) register_5 (
    .D({{11{1'b1}}, nRead_Write, Mask, Address}), .en(Chip_Select), .Q(register_5_q), .clk(CLK),
    .clr(or_9_out));
  or or_9 (or_9_out, ~Chip_Select, Reset);  // OR_Gate
  D_Flip_Flop Proc (.clk(CLK), .D(or_4_out), .Q(Proc_q), .reset(or_10_out));  // open: Qn, preset, en
  or or_10 (or_10_out, ~Chip_Select, Reset);  // OR_Gate
  Demultiplexer #(.enable("false")) demultiplexer_2 (
    .out0(Count), .out1(Update_Mem), .in(demultiplexer_3_out0), .sel(Zero_Time));
  Demultiplexer #(.enable("false")) demultiplexer_3 (
    .out0(demultiplexer_3_out0), .out1(Load1), .in(Proc_q), .sel(Changed));
  Clock clock_1 (.out(CLK));
  Comparator #(.width(32)) comparator_2 (.a(register_1_q), .b(Data_In_0), .eq(comparator_2_eq));  // open: gt, lt
  Comparator #(.width(32)) comparator_3 (.a(register_2_q), .b(Data_In_1), .eq(comparator_3_eq));  // open: gt, lt
  Comparator #(.width(32)) comparator_4 (.a(register_3_q), .b(Data_In_2), .eq(comparator_4_eq));  // open: gt, lt
  Comparator #(.width(32)) comparator_5 (.a(register_4_q), .b(Data_In_3), .eq(comparator_5_eq));  // open: gt, lt
  Comparator #(.width(32)) comparator_6 (
    .a(register_5_q), .b({{11{1'b1}}, nRead_Write, Mask, Address}), .eq(comparator_6_eq));  // open: gt, lt
  nand nand_1 (nand_1_out, comparator_6_eq, comparator_2_eq, comparator_3_eq, comparator_4_eq, comparator_5_eq);
  and and_1 (Changed, nand_1_out, Chip_Select);
  or or_11 (Load, Count, Load1, Load0);
  and and_2 (and_2_out, Mask[0], Update_Mem, nRead_Write);
  and and_3 (and_3_out, Mask[1], Update_Mem, nRead_Write);
  and and_4 (and_4_out, Mask[2], Update_Mem, nRead_Write);
  and and_5 (and_5_out, Mask[3], Update_Mem, nRead_Write);
  RAM_part #(.addrWidth(16), .dataWidth(32), .bus("separate")) ram_1 (
    .addr(Address), .din(Data_In_0), .data(Data_Out_0), .str(and_2_out), .sel(Chip_Select), .clk(CLK),
    .ld(and_6_out), .clr(Reset));
  and and_6 (and_6_out, ~nRead_Write, Idle);  // AND_Gate
  RAM_part #(.addrWidth(16), .dataWidth(32), .bus("separate")) ram_2 (
    .addr(Address), .din(Data_In_1), .data(Data_Out_1), .str(and_3_out), .sel(Chip_Select), .clk(CLK),
    .ld(and_7_out), .clr(Reset));
  and and_7 (and_7_out, ~nRead_Write, Idle);  // AND_Gate
  RAM_part #(.addrWidth(16), .dataWidth(32), .bus("separate")) ram_3 (
    .addr(Address), .din(Data_In_2), .data(Data_Out_2), .str(and_4_out), .sel(Chip_Select), .clk(CLK),
    .ld(and_8_out), .clr(Reset));
  and and_8 (and_8_out, ~nRead_Write, Idle);  // AND_Gate
  RAM_part #(.addrWidth(16), .dataWidth(32), .bus("separate")) ram_4 (
    .addr(Address), .din(Data_In_3), .data(Data_Out_3), .str(and_5_out), .sel(Chip_Select), .clk(CLK),
    .ld(and_9_out), .clr(Reset));
  and and_9 (and_9_out, ~nRead_Write, Idle);  // AND_Gate

  assign Read_Time = 4'b0011;
  assign Write_Time = 4'b0010;

  // Other names for the same wires on the sheet: M0 = Mask[0]; M1 = Mask[1]; M2 = Mask[2]; M3 = Mask[3];
  //   RW = nRead_Write; CLR = Reset; CS = Chip_Select; Load2 = Count

  // Notes on the sheet:
  //   NO MODIFICAR
  //   excepto quizás los valores RT y WT
  //   BANK0
  //   BANK1
  //   BANK2
  //   BANK3
endmodule

module S_MIPS (
  input  Kbd_Available,
  input  [6:0] Kbd_ASCII_Data,
  input  [31:0] RAM_Out_0,
  input  [31:0] RAM_Out_1,
  input  Reset,
  input  [31:0] RAM_Out_2,
  input  Clock,
  input  [31:0] RAM_Out_3,
  input  [3:0] Read_Time,
  input  [3:0] Write_Time,
  output Kbd_Enable,
  output [15:0] Address,
  output Kbd_Clear,
  output TTY_Enable,
  output [6:0] TTY_ASCII_Data,
  output Stop,
  output [31:0] RAM_In_0,
  output [31:0] RAM_In_1,
  output [31:0] RAM_In_2,
  output [31:0] RAM_In_3,
  output [3:0] Mask,
  output nRead_Write,
  output Chip_Select
);

  wire and_1_out, EN, EN_Branch, Enable_LW, Execute, Load_Instruction, Mem_End, Rt_S, Save;
  wire [1:0] Address_To_Mem;
  wire [2:0] SM_INSTRUCTION;
  wire [31:0] Address_in, Memory_Out, Registro;

  Control_Unit control_unit_1 (
    .Reset(Reset), .CLK(Clock), .Mem_End(Mem_End), .Instruction(SM_INSTRUCTION), .CS(Chip_Select),
    .R_W(nRead_Write), .Load_Instruction(Load_Instruction), .EN_Datapath(EN),
    .Adress_To_Memory(Address_To_Mem), .Enable_Datapath_Branch(EN_Branch), .Register_Data_Rt(Rt_S),
    .halt(Stop), .Execute(Execute), .Enable_LW(Enable_LW));
  Memory_Manager memory_manager_1 (
    .CS(Chip_Select), .CLK(Clock), .CLR(Reset), .R_W_Time_Selector(nRead_Write), .Read_Time(Read_Time),
    .Write_Time(Write_Time), .Address_In(Address_in), .Register(Registro), .RAM_out_0(RAM_Out_0),
    .RAM_out_1(RAM_Out_1), .RAM_out_2(RAM_Out_2), .RAM_massk(Mask), .RAM_out_3(RAM_Out_3),
    .RAM_in_0(RAM_In_0), .RAM_in_1(RAM_In_1), .RAM_in_2(RAM_In_2), .RAM_in_3(RAM_In_3), .Out(Memory_Out),
    .Address(Address), .Ready(Mem_End), .RST(Reset), .Save(Save));
  // Probe on Address_To_Mem
  and and_1 (and_1_out, Load_Instruction, Save);
  Datapath datapath_1 (
    .Data(Memory_Out), .clk(Clock), .clr(Reset), .EN(EN), .Memory_Data(Memory_Out), .registro(Registro),
    .halt(Stop), .Mem_Dir(Address_in), .Branch_EN(EN_Branch), .Register_Data_Rt(Rt_S),
    .Adress_To_Memory(Address_To_Mem), .Load_Instruction(and_1_out), .kbd_data(Kbd_ASCII_Data),
    .kbd_aviable(Kbd_Available), .SM_Instruction(SM_INSTRUCTION), .tty_data(TTY_ASCII_Data),
    .Kbd_Enable(Kbd_Enable), .tty_enable(TTY_Enable), .Execute(Execute), .Save_Mem(Save),
    .Write_Enable(Enable_LW));

  assign Kbd_Clear = Kbd_Available;

  // Other names for the same wires on the sheet: CLK = Clock; CLR = Reset; CS = Chip_Select; halt = Stop;
  //   KBD_AVAIL = Kbd_Available; KBD_DATA[6:0] = Kbd_ASCII_Data; RAM_A[15:0] = Address; RAM_INPUT_0[31:0] = RAM_In_0;
  //   RAM_INPUT_1[31:0] = RAM_In_1; RAM_INPUT_2[31:0] = RAM_In_2; RAM_INPUT_3[31:0] = RAM_In_3; RAM_MASK[3:0] = Mask;
  //   RAM_OUTPUT_0[31:0] = RAM_Out_0; RAM_OUTPUT_1[31:0] = RAM_Out_1; RAM_OUTPUT_2[31:0] = RAM_Out_2;
  //   RAM_OUTPUT_3[31:0] = RAM_Out_3; RW = nRead_Write; TTY_DATA[6:0] = TTY_ASCII_Data

  // Notes on the sheet:
  //   RAM ADDRESS
  //   DATA FROM RAM
  //   DATA TO RAM
  //   DATA WRITE MASK
  //   RAM TIMING
  //   RAM CONTROL
  //   KEYBOARD
  //   TTY
  //   SEQUENCING
endmodule

module RAM_Dispatcher (
  input  [3:0] WriteTime,
  input  Clock,
  input  CLR,
  output [31:0] Data,
  output [15:0] Address,
  output [3:0] Mask,
  output Finished,
  output Write
);

  wire demultiplexer_2_out1, demultiplexer_3_out1, End, IDLE_q, IncAddr, Load, or_1_out, or_2_out, While_q,
       WriteEnd;
  wire [3:0] counter_1_q;
  wire [31:0] CurrentAddress_q;

  Counter #(.width(32), .max('hffffffff)) CurrentAddress (
    .count(IncAddr), .Q({CurrentAddress_q[31:18], Address, CurrentAddress_q[1:0]}), .clk(Clock), .clr(CLR));  // open: load, D, carry
  or or_1 (or_1_out, IncAddr, demultiplexer_3_out1, Finished);
  D_Flip_Flop IDLE (.clk(Clock), .D(or_1_out), .Q(IDLE_q), .preset(CLR));  // open: Qn, en, reset
  Demultiplexer #(.enable("false")) demultiplexer_1 (.out0(Load), .out1(Finished), .in(IDLE_q), .sel(End));
  D_Flip_Flop While (.clk(Clock), .D(or_2_out), .Q(While_q), .reset(CLR));  // open: Qn, preset, en
  or or_2 (or_2_out, Write, Load);
  RAM_part #(.addrWidth(18), .dataWidth(32)) ram_1 (
    .addr({Address, CurrentAddress_q[1:0]}), .data(Data), .clk(Clock));  // open: sel, ld, clr
  Demultiplexer #(.enable("false")) demultiplexer_2 (
    .out0(Write), .out1(demultiplexer_2_out1), .in(While_q), .sel(WriteEnd));
  Decoder #(.select(2)) decoder_1 (
    .out0(Mask[0]), .out1(Mask[1]), .out2(Mask[2]), .out3(Mask[3]), .sel(CurrentAddress_q[1:0]));  // open: en
  Demultiplexer #(.enable("false")) demultiplexer_3 (
    .out0(IncAddr), .out1(demultiplexer_3_out1), .in(demultiplexer_2_out1), .sel(End));
  Counter #(.width(4), .max('hf)) counter_1 (
    .load(Load), .D(WriteTime), .count(Write), .Q(counter_1_q), .clk(Clock));  // open: carry, clr
  Comparator #(.width(32)) comparator_1 (.a(Data), .b({32{1'b1}}), .eq(End));  // open: gt, lt
  Comparator #(.width(4)) comparator_2 (.a(4'b0000), .b(counter_1_q), .eq(WriteEnd));  // open: gt, lt

  // Other names for the same wires on the sheet: CLK = Clock; Count = Write; WT[3:0] = WriteTime
endmodule

module Register_File (
  input  Clock,
  input  [4:0] Rs,
  input  [31:0] Hi_in,
  input  [4:0] Rt,
  input  [4:0] Rd,
  input  [31:0] Lo_in,
  input  [31:0] Write_Data,
  input  Clear,
  input  Mul_Div,
  input  pop,
  input  push,
  input  EN,
  output [31:0] Hi_out,
  output [31:0] Lo_out,
  output [31:0] Read_Data_1,
  output [31:0] Read_Data_2,
  output [31:0] SP
);

  wire and_1_out, and_5_out, or_2_out, R0_Wreg, R1_Wreg, R2_Wreg, R3_Wreg, R4_Wreg, R5_Wreg, R6_Wreg,
       R7_Wreg, R8_Wreg, R9_Wreg, R10_Wreg, R11_Wreg, R12_Wreg, R13_Wreg, R14_Wreg, R15_Wreg, R16_Wreg,
       R17_Wreg, R18_Wreg, R19_Wreg, R20_Wreg, R21_Wreg, R22_Wreg, R23_Wreg, R24_Wreg, R25_Wreg, R26_Wreg,
       R27_Wreg, R28_Wreg, R29_Wreg, R30_Wreg, R31_Wreg, Sp_Save, Stack;
  wire [31:0] adder_1_out, adder_2_out, and_3_out, and_4_out, multiplexer_1_out, multiplexer_2_out, R1, R2,
       R3, R4, R5, R6, R7, R8, R9, R10, R11, R12, R13, R14, R15, R16, R17, R18, R19, R20, R21, R22, R23, R24,
       R25, R26, R27, R28, R29, R30, Sp_Input;

  Multiplexer #(.width(32), .enable("false")) multiplexer_1 (
    .in0(32'hfffffffc), .in1(32'h4), .out(multiplexer_1_out), .sel(pop));
  or or_1 (Stack, pop, push);
  Adder #(.width(32)) adder_1 (.a(SP), .b(multiplexer_1_out), .out(adder_1_out));  // open: cin, cout
  Multiplexer #(.width(32), .enable("false")) multiplexer_2 (
    .in0(Write_Data), .in1(adder_1_out), .out(multiplexer_2_out), .sel(and_1_out));
  and and_1 (and_1_out, Stack, ~R31_Wreg);  // AND_Gate
  or or_2 (or_2_out, R31_Wreg, Stack);
  and and_2 (Sp_Save, or_2_out, EN);
  assign and_3_out = multiplexer_2_out & 32'hfffffffc;  // AND_Gate and_3, 32 bits wide
  assign and_4_out = Write_Data & 32'hfffffffc;  // AND_Gate and_4, 32 bits wide
  Register #(.width(32)) register_1 (.D(Hi_in), .en(Mul_Div), .Q(Hi_out), .clk(Clock), .clr(Clear));
  Register #(.width(32)) register_2 (.D(Lo_in), .en(Mul_Div), .Q(Lo_out), .clk(Clock), .clr(Clear));
  Adder #(.width(32)) adder_2 (.a(and_4_out), .b(32'h4), .out(adder_2_out));  // open: cin, cout
  Multiplexer #(.width(32), .enable("false")) multiplexer_3 (
    .in0(and_3_out), .in1(adder_2_out), .out(Sp_Input), .sel(and_5_out));
  and and_5 (and_5_out, pop, R31_Wreg);
  Multiplexer #(.select(5), .width(32)) multiplexer_4 (
    .in0({32{1'b0}}), .in1(R1), .in2(R2), .in3(R3), .in4(R4), .in5(R5), .in6(R6), .in7(R7), .in8(R8),
    .in9(R9), .in10(R10), .in11(R11), .in12(R12), .in13(R13), .in14(R14), .in15(R15), .in16(R16), .in17(R17),
    .in18(R18), .in19(R19), .in20(R20), .in21(R21), .in22(R22), .in23(R23), .in24(R24), .in25(R25),
    .in26(R26), .in27(R27), .in28(R28), .in29(R29), .in30(R30), .in31(SP), .out(Read_Data_1), .sel(Rs));  // open: en
  Multiplexer #(.select(5), .width(32)) multiplexer_5 (
    .in0({32{1'b0}}), .in1(R1), .in2(R2), .in3(R3), .in4(R4), .in5(R5), .in6(R6), .in7(R7), .in8(R8),
    .in9(R9), .in10(R10), .in11(R11), .in12(R12), .in13(R13), .in14(R14), .in15(R15), .in16(R16), .in17(R17),
    .in18(R18), .in19(R19), .in20(R20), .in21(R21), .in22(R22), .in23(R23), .in24(R24), .in25(R25),
    .in26(R26), .in27(R27), .in28(R28), .in29(R29), .in30(R30), .in31(SP), .out(Read_Data_2), .sel(Rt));  // open: en
  Decoder #(.select(5)) decoder_1 (
    .out0(R0_Wreg), .out1(R1_Wreg), .out2(R2_Wreg), .out3(R3_Wreg), .out4(R4_Wreg), .out5(R5_Wreg),
    .out6(R6_Wreg), .out7(R7_Wreg), .out8(R8_Wreg), .out9(R9_Wreg), .out10(R10_Wreg), .out11(R11_Wreg),
    .out12(R12_Wreg), .out13(R13_Wreg), .out14(R14_Wreg), .out15(R15_Wreg), .out16(R16_Wreg),
    .out17(R17_Wreg), .out18(R18_Wreg), .out19(R19_Wreg), .out20(R20_Wreg), .out21(R21_Wreg),
    .out22(R22_Wreg), .out23(R23_Wreg), .out24(R24_Wreg), .out25(R25_Wreg), .out26(R26_Wreg),
    .out27(R27_Wreg), .out28(R28_Wreg), .out29(R29_Wreg), .out30(R30_Wreg), .out31(R31_Wreg), .sel(Rd));  // open: en
  Register #(.width(32)) R (.D(Write_Data), .en(R1_Wreg), .Q(R1), .clk(Clock), .clr(Clear));
  Register #(.width(32)) R_2 (.D(Write_Data), .en(R2_Wreg), .Q(R2), .clk(Clock), .clr(Clear));
  Register #(.width(32)) R_3 (.D(Write_Data), .en(R3_Wreg), .Q(R3), .clk(Clock), .clr(Clear));
  Register #(.width(32)) R_4 (.D(Write_Data), .en(R4_Wreg), .Q(R4), .clk(Clock), .clr(Clear));
  Register #(.width(32)) R_5 (.D(Write_Data), .en(R5_Wreg), .Q(R5), .clk(Clock), .clr(Clear));
  Register #(.width(32)) R_6 (.D(Write_Data), .en(R6_Wreg), .Q(R6), .clk(Clock), .clr(Clear));
  Register #(.width(32)) R_7 (.D(Write_Data), .en(R7_Wreg), .Q(R7), .clk(Clock), .clr(Clear));
  Register #(.width(32)) R_8 (.D(Write_Data), .en(R8_Wreg), .Q(R8), .clk(Clock), .clr(Clear));
  Register #(.width(32)) R_9 (.D(Write_Data), .en(R9_Wreg), .Q(R9), .clk(Clock), .clr(Clear));
  Register #(.width(32)) R_10 (.D(Write_Data), .en(R10_Wreg), .Q(R10), .clk(Clock), .clr(Clear));
  // Probe on R3
  Register #(.width(32)) R_11 (.D(Write_Data), .en(R11_Wreg), .Q(R11), .clk(Clock), .clr(Clear));
  Register #(.width(32)) R_12 (.D(Write_Data), .en(R12_Wreg), .Q(R12), .clk(Clock), .clr(Clear));
  Register #(.width(32)) R_13 (.D(Write_Data), .en(R13_Wreg), .Q(R13), .clk(Clock), .clr(Clear));
  Register #(.width(32)) R_14 (.D(Write_Data), .en(R14_Wreg), .Q(R14), .clk(Clock), .clr(Clear));
  Register #(.width(32)) R_15 (.D(Write_Data), .en(R15_Wreg), .Q(R15), .clk(Clock), .clr(Clear));
  Register #(.width(32)) R_16 (.D(Write_Data), .en(R16_Wreg), .Q(R16), .clk(Clock), .clr(Clear));
  Register #(.width(32)) R_17 (.D(Write_Data), .en(R17_Wreg), .Q(R17), .clk(Clock), .clr(Clear));
  Register #(.width(32)) R_18 (.D(Write_Data), .en(R18_Wreg), .Q(R18), .clk(Clock), .clr(Clear));
  Register #(.width(32)) R_19 (.D(Write_Data), .en(R19_Wreg), .Q(R19), .clk(Clock), .clr(Clear));
  Register #(.width(32)) R_20 (.D(Write_Data), .en(R20_Wreg), .Q(R20), .clk(Clock), .clr(Clear));
  Register #(.width(32)) R_21 (.D(Write_Data), .en(R21_Wreg), .Q(R21), .clk(Clock), .clr(Clear));
  Register #(.width(32)) R_22 (.D(Write_Data), .en(R23_Wreg), .Q(R22), .clk(Clock), .clr(Clear));
  Register #(.width(32)) R_23 (.D(Write_Data), .en(R23_Wreg), .Q(R23), .clk(Clock), .clr(Clear));
  Register #(.width(32)) R_24 (.D(Write_Data), .en(R24_Wreg), .Q(R24), .clk(Clock), .clr(Clear));
  Register #(.width(32)) R_25 (.D(Write_Data), .en(R25_Wreg), .Q(R25), .clk(Clock), .clr(Clear));
  Register #(.width(32)) R_26 (.D(Write_Data), .en(R26_Wreg), .Q(R26), .clk(Clock), .clr(Clear));
  Register #(.width(32)) R_27 (.D(Write_Data), .en(R27_Wreg), .Q(R27), .clk(Clock), .clr(Clear));
  Register #(.width(32)) R_28 (.D(Write_Data), .en(R28_Wreg), .Q(R28), .clk(Clock), .clr(Clear));
  Register #(.width(32)) R_29 (.D(Write_Data), .en(R29_Wreg), .Q(R29), .clk(Clock), .clr(Clear));
  Register #(.width(32)) R_30 (.D(Write_Data), .en(R30_Wreg), .Q(R30), .clk(Clock), .clr(Clear));
  Register #(.width(32)) R_31 (.D(Sp_Input), .en(Sp_Save), .Q(SP), .clk(Clock), .clr(Clear));

  // Other names for the same wires on the sheet: CLK = Clock; WData[31:0] = Write_Data

  // Notes on the sheet:
  //   Stack Pointer Implementation
  //   aproximacion a 4*x
  //   aproximacion a 4*x
  //   Hi-Lo Implementation
  //   Registers
endmodule

module Instruction_Decoder (
  input  [31:0] Instruction,
  output nop,
  output tty,
  output [6:0] Branch__I,
  output [2:0] SM_Instruction,
  output halt,
  output rnd,
  output kbd,
  output [3:0] alu_operator,
  output [27:0] destino,
  output [4:0] Rs,
  output pop,
  output push,
  output logic_i,
  output [4:0] Rt,
  output lw,
  output sw,
  output [4:0] Rd,
  output mul_div,
  output [31:0] Logic_Op,
  output [31:0] Aritmetic_Op,
  output [31:0] Branch,
  output load_zero,
  output RF_zero,
  output [1:0] data_to_RF,
  output inmediate,
  output load_Rd
);

  wire a, add, add_i, ai, \and , and_17_out, and_18_out, and_19_out, and_20_out, and_24_out, and_29_out,
       and_30_out, and_i, branch_t, div, div_u, func_code____0, func_code____1, func_code____011, lw_sw,
       mfhi, mflo, mul, mul_u, \nor , op_code____0, op_code____1, opp_aritmetica, \or , or_2_out, or_9_out,
       or_10_out, or_11_out, or_12_out, or_13_out, or_14_out, or_15_out, or_i, pop_push, slt, slt_i, slt_u,
       sltu_i, sub, \xor , xor_i;

  and and_1 (func_code____1, Instruction[0], Instruction[1], Instruction[2], Instruction[3], Instruction[4], Instruction[5]);
  and and_2 (func_code____0, ~Instruction[0], ~Instruction[1], ~Instruction[2], ~Instruction[3], ~Instruction[4], ~Instruction[5]);  // AND_Gate
  and and_3 (op_code____1, Instruction[26], Instruction[27], Instruction[28], Instruction[29], Instruction[30], Instruction[31]);
  and and_4 (op_code____0, ~Instruction[26], ~Instruction[27], ~Instruction[28], ~Instruction[29], ~Instruction[30], ~Instruction[31]);  // AND_Gate
  and and_5 (branch_t, ~Instruction[29], ~Instruction[30], ~Instruction[31], ~op_code____0);  // AND_Gate
  and and_6 (pop_push, ~Instruction[26], ~Instruction[27], ~Instruction[28], Instruction[29], Instruction[30], Instruction[31]);  // AND_Gate
  and and_7 (func_code____011, Instruction[3], Instruction[4], ~Instruction[5]);  // AND_Gate
  or or_1 (lw_sw, lw, sw);
  and and_8 (halt, op_code____1, func_code____1);
  and and_9 (nop, op_code____0, func_code____0);
  and and_10 (ai, opp_aritmetica, inmediate);
  and and_11 (add_i, ~Instruction[26], ~Instruction[27], ~Instruction[28], ai);  // AND_Gate
  and and_12 (slt_i, ~Instruction[26], Instruction[27], ~Instruction[28], ai);  // AND_Gate
  and and_13 (sltu_i, Instruction[26], Instruction[27], ~Instruction[28], ai);  // AND_Gate
  Priority_Encoder #(.select(2)) priority_encoder_1 (
    .in0(1'b1), .in1(mfhi), .in2(mflo), .in3(or_2_out), .out(data_to_RF));  // open: gs, en_out, en_in
  or or_2 (or_2_out, pop, lw);
  and and_14 (and_i, ~Instruction[26], ~Instruction[27], Instruction[28], ai);  // AND_Gate
  and and_15 (or_i, Instruction[26], ~Instruction[27], Instruction[28], ai);  // AND_Gate
  and and_16 (xor_i, ~Instruction[26], Instruction[27], Instruction[28], ai);  // AND_Gate
  and and_17 (and_17_out, Instruction[29], ~Instruction[30], ~Instruction[31]);  // AND_Gate
  and and_18 (and_18_out, Instruction[29], ~Instruction[30], ~Instruction[31]);  // AND_Gate
  or or_3 (RF_zero, Branch__I[6], Branch__I[4], Branch__I[5]);
  and and_19 (and_19_out, opp_aritmetica, ~inmediate);  // AND_Gate
  and and_20 (and_20_out, ~load_Rd, ~inmediate);  // AND_Gate
  and and_21 (tty, op_code____1, ~halt, Instruction[0]);  // AND_Gate
  and and_22 (rnd, op_code____1, ~halt, Instruction[1]);  // AND_Gate
  and and_23 (kbd, op_code____1, ~halt, Instruction[2]);  // AND_Gate
  or or_4 (opp_aritmetica, and_17_out, and_24_out);
  and and_24 (and_24_out, op_code____0, ~nop, ~mfhi, ~mflo, ~Branch__I[1], ~func_code____011);  // AND_Gate
  or or_5 (inmediate, and_18_out, lw, sw);
  or or_6 (load_Rd, and_19_out, rnd, mflo, pop, mfhi, kbd);
  or or_7 (load_zero, and_20_out, sw);
  or or_8 (logic_i, and_i, or_i, xor_i);
  Priority_Encoder priority_encoder_2 (
    .in0(1'b1), .in1(pop), .in2(push), .in3(lw), .in4(sw), .out(SM_Instruction));  // open: in5, in6, in7, en_in, gs, en_out
  and and_25 (mfhi, op_code____0, ~Instruction[0], ~Instruction[1], ~Instruction[2], ~Instruction[3], Instruction[4], ~Instruction[5]);  // AND_Gate
  and and_26 (mflo, op_code____0, ~Instruction[0], Instruction[1], ~Instruction[2], ~Instruction[3], Instruction[4], ~Instruction[5]);  // AND_Gate
  and and_27 (lw, Instruction[26], Instruction[27], ~Instruction[28], ~Instruction[29], ~Instruction[30], Instruction[31]);  // AND_Gate
  or or_9 (or_9_out, add, add_i, lw_sw);
  or or_10 (or_10_out, branch_t, sub);
  or or_11 (or_11_out, slt, slt_i);
  or or_12 (or_12_out, slt_u, sltu_i);
  or or_13 (or_13_out, \and , and_i);
  or or_14 (or_14_out, \or , or_i);
  or or_15 (or_15_out, \xor , xor_i);
  Priority_Encoder #(.select(4)) priority_encoder_3 (
    .in0(or_9_out), .in1(or_10_out), .in2(mul), .in3(mul_u), .in4(div), .in5(div_u), .in6(or_11_out),
    .in7(or_12_out), .in8(or_13_out), .in9(or_14_out), .in10(\nor ), .in11(or_15_out), .out(alu_operator));  // open: in12, in13, in14, in15, gs, en_out, en_in
  and and_28 (sw, Instruction[26], Instruction[27], ~Instruction[28], Instruction[29], ~Instruction[30], Instruction[31]);  // AND_Gate
  and and_29 (and_29_out, op_code____0, func_code____011);
  or or_16 (a, and_29_out, and_30_out);
  and and_30 (and_30_out, opp_aritmetica, op_code____0);
  or or_17 (mul_div, mul, mul_u, div, div_u);
  and and_31 (Branch__I[0], ~Instruction[26], Instruction[27], ~Instruction[28], ~Instruction[29], ~Instruction[30], ~Instruction[31]);  // AND_Gate
  and and_32 (Branch__I[1], op_code____0, ~Instruction[0], ~Instruction[1], ~Instruction[2], Instruction[3], ~Instruction[4], ~Instruction[5]);  // AND_Gate
  and and_33 (Branch__I[2], ~Instruction[26], ~Instruction[27], Instruction[28], branch_t);  // AND_Gate
  and and_34 (Branch__I[3], Instruction[26], ~Instruction[27], Instruction[28], branch_t);  // AND_Gate
  and and_35 (add, a, ~Instruction[0], ~Instruction[1], ~Instruction[2], ~Instruction[3], ~Instruction[4], Instruction[5]);  // AND_Gate
  and and_36 (sub, a, ~Instruction[0], Instruction[1], ~Instruction[2], ~Instruction[3], ~Instruction[4], Instruction[5]);  // AND_Gate
  and and_37 (mul, a, ~Instruction[0], ~Instruction[1], ~Instruction[2], Instruction[3], Instruction[4], ~Instruction[5]);  // AND_Gate
  and and_38 (mul_u, a, Instruction[0], ~Instruction[1], ~Instruction[2], Instruction[3], Instruction[4], ~Instruction[5]);  // AND_Gate
  and and_39 (\and , a, ~Instruction[0], ~Instruction[1], Instruction[2], ~Instruction[3], ~Instruction[4], Instruction[5]);  // AND_Gate
  and and_40 (\or , a, Instruction[0], ~Instruction[1], Instruction[2], ~Instruction[3], ~Instruction[4], Instruction[5]);  // AND_Gate
  and and_41 (Branch__I[6], ~Instruction[26], Instruction[27], Instruction[28], branch_t);  // AND_Gate
  and and_42 (pop, pop_push, func_code____0);
  and and_43 (Branch__I[4], Instruction[26], Instruction[27], Instruction[28], branch_t);
  and and_44 (Branch__I[5], Instruction[26], ~Instruction[27], ~Instruction[28], branch_t);  // AND_Gate
  assign Aritmetic_Op[31:16] = {{15{Instruction[15]}}, Instruction[15]};  // Bit_Extender bit_extender_1
  assign Branch[31:18] = {{13{Instruction[15]}}, Instruction[15]};  // Bit_Extender bit_extender_2
  and and_45 (div, a, ~Instruction[0], Instruction[1], ~Instruction[2], Instruction[3], Instruction[4], ~Instruction[5]);  // AND_Gate
  and and_46 (div_u, a, Instruction[0], Instruction[1], ~Instruction[2], Instruction[3], Instruction[4], ~Instruction[5]);  // AND_Gate
  and and_47 (slt, a, ~Instruction[0], Instruction[1], ~Instruction[2], Instruction[3], ~Instruction[4], Instruction[5]);  // AND_Gate
  and and_48 (slt_u, a, Instruction[0], Instruction[1], ~Instruction[2], Instruction[3], ~Instruction[4], Instruction[5]);  // AND_Gate
  and and_49 (\nor , a, Instruction[0], Instruction[1], Instruction[2], ~Instruction[3], ~Instruction[4], Instruction[5]);  // AND_Gate
  and and_50 (\xor , a, ~Instruction[0], ~Instruction[1], ~Instruction[2], Instruction[3], ~Instruction[4], Instruction[5]);  // AND_Gate
  and and_51 (push, pop_push, Instruction[0], ~Instruction[1], ~Instruction[2], ~Instruction[3], ~Instruction[4], ~Instruction[5]);  // AND_Gate

  assign Aritmetic_Op[15:0] = Instruction[15:0];
  assign Branch[17:0] = {Instruction[15:0], 2'b00};
  assign destino = {Instruction[25:0], 2'b00};
  assign Logic_Op = {{16{1'b0}}, Instruction[15:0]};
  assign Rd = Instruction[15:11];
  assign Rs = Instruction[25:21];
  assign Rt = Instruction[20:16];

  // Other names for the same wires on the sheet: alu_operador[3:0] = alu_operator; constant[15:0] = Instruction[15:0];
  //   destiny[25:0] = Instruction[25:0]; func_code[5:0] = Instruction[5:0]; Branch_I[6:0] = Branch__I;
  //   j = Branch__I[0]; jr = Branch__I[1]; be = Branch__I[2]; bne = Branch__I[3]; bgtz = Branch__I[4];
  //   bltz = Branch__I[5]; blez = Branch__I[6]; op_code[5:0] = Instruction[31:26]

  // Notes on the sheet:
  //   INPUT
  //   DECODER
  //   GENERAL
  //   INMEDIATE
  //   MFHI && MFLO
  //   LOAD/STORE WORD
  //   JUMP
  //   ARITMETIC
  //   INSTRUCTION DECODER
  //   OUTPUTS
  //   BRANCH
  //   POP/PUSH
  //   BRANCH
endmodule

module ALU (
  input  [31:0] A,
  input  [31:0] B,
  input  [3:0] S,
  output [31:0] R,
  output [31:0] hi,
  output zero,
  output [31:0] lo,
  output neg
);

  wire comparator_2_lt, comparator_3_lt, HL0;
  wire [31:0] ADD, AND, DIVS_HI, DIVS_LO, DIVU_HI, DIVU_LO, MULT_HI, MULT_LO, MULU_HI, MULU_LO, NOR, OR, SLT,
       SLTU, SUB, XOR;

  // Probe on A
  Adder #(.width(32)) adder_1 (.a(A), .b(B), .out(ADD));  // open: cin, cout
  Subtractor #(.width(32)) subtractor_1 (.a(A), .b(B), .out(SUB));  // open: bin, bout
  assign OR = A | B;  // OR_Gate or_1, 32 bits wide
  assign AND = A & B;  // AND_Gate and_1, 32 bits wide
  Multiplexer #(.select(2), .width(32), .enable("false")) multiplexer_1 (
    .in0(MULT_HI), .in1(MULU_HI), .in2(DIVS_HI), .in3(DIVU_HI), .out(hi), .sel({HL0, S[0]}));
  or or_2 (HL0, S[2], S[3]);
  // Probe on B
  Multiplier #(.width(32)) multiplier_1 (.a(A), .b(B), .out(MULT_LO), .cout(MULT_HI));  // open: cin
  Divider #(.width(32)) divider_1 (.a(A), .b(B), .out(DIVU_LO), .rem(DIVU_HI));  // open: upper
  assign NOR = ~(A | B);  // NOR_Gate nor_1, 32 bits wide
  assign XOR = A ^ B;  // XOR_Gate xor_1, 32 bits wide
  // Probe on lo
  Comparator #(.width(32)) comparator_1 (.a(lo), .b({32{1'b0}}), .eq(zero), .lt(neg));  // open: gt
  DivS divs_1 (.A(A), .B(B), .LowOutput(DIVS_LO), .HighOutput(DIVS_HI));
  MulU mulu_1 (.in_1(A), .in_2(B), .low(MULU_LO), .hi(MULU_HI));
  Multiplexer #(.width(32), .enable("false")) multiplexer_2 (
    .in0({32{1'b0}}), .in1(32'h1), .out(SLT), .sel(comparator_2_lt));
  Comparator #(.width(32)) comparator_2 (.a(A), .b(B), .lt(comparator_2_lt));  // open: gt, eq
  Multiplexer #(.width(32), .enable("false")) multiplexer_3 (
    .in0({32{1'b0}}), .in1(32'h1), .out(SLTU), .sel(comparator_3_lt));
  Comparator #(.width(32), .mode("unsigned")) comparator_3 (.a(A), .b(B), .lt(comparator_3_lt));  // open: gt, eq
  Multiplexer #(.select(4), .width(32), .enable("false")) multiplexer_4 (
    .in0(ADD), .in1(SUB), .in2(MULT_LO), .in3(MULU_LO), .in4(DIVS_LO), .in5(DIVU_LO), .in6(SLT), .in7(SLTU),
    .in8(AND), .in9(OR), .in10(NOR), .in11(XOR), .out(lo), .sel(S));  // open: in12, in13, in14, in15
  // Probe on hi

  assign R = lo;

  // Other names for the same wires on the sheet: RESULT[31:0] = lo; HL = S[0]; SELECT[3:0] = S

  // Notes on the sheet:
  //   ARITMÉTICA
  //   LÓGICA
  //   INPUTS
  //   MULT
  //   DIVU
  //   HILO SELECTOR
  //   COMPARACIÓN
  //   0000
  //   0001
  //   0010
  //   0011
  //   0100
  //   0101
  //   0110
  //   0111
  //   1000
  //   1001
  //   1010
  //   1011
  //   OUTPUTS
  //   OPERATION SELECTOR
endmodule

module DivS (
  input  [31:0] A,
  input  [31:0] B,
  output [31:0] LowOutput,
  output [31:0] HighOutput
);

  wire xor_1_out;
  wire [31:0] divider_1_out, multiplexer_1_out, multiplexer_2_out, negator_1_out, negator_2_out,
       negator_3_out;

  Negator #(.width(32)) negator_1 (.in(A), .out(negator_1_out));
  Negator #(.width(32)) negator_2 (.in(B), .out(negator_2_out));
  Multiplexer #(.width(32), .enable("false")) multiplexer_1 (
    .in0(A), .in1(negator_1_out), .out(multiplexer_1_out), .sel(A[31]));
  Multiplexer #(.width(32), .enable("false")) multiplexer_2 (
    .in0(B), .in1(negator_2_out), .out(multiplexer_2_out), .sel(B[31]));
  Divider #(.width(32)) divider_1 (
    .a(multiplexer_1_out), .b(multiplexer_2_out), .out(divider_1_out), .rem(HighOutput));  // open: upper
  Negator #(.width(32)) negator_3 (.in(divider_1_out), .out(negator_3_out));
  xor xor_1 (xor_1_out, A[31], B[31]);
  // Probe on LowOutput
  Multiplexer #(.width(32), .enable("false")) multiplexer_3 (
    .in0(divider_1_out), .in1(negator_3_out), .out(LowOutput), .sel(xor_1_out));
  // Probe on HighOutput

  // Notes on the sheet:
  //   SIGNED DIV
endmodule

module MulU (
  input  [31:0] in_1,
  input  [31:0] in_2,
  output [31:0] low,
  output [31:0] hi
);

  wire C_S_low1, C_S_low2, C_S_low3, carry, carry2, S3;
  wire [31:0] A_S2, AL, AR, ARxBR_hi, ARxBR_low, B_S1, bit_extender_1_out, bit_extender_2_out,
       bit_extender_3_out, bit_extender_4_out, BL, BR, hi1, hi2, low1, low2, S_hi1, S_hi2, S_low1, S_low2;

  // Probe on in_1
  Shift shift_1 (.in_1(1'b0), .in_2(ARxBR_low), .Output0(carry), .Output(low1));
  Shift shift_2 (.in_1(1'b0), .in_2(low1), .Output0(carry2), .Output(low2));
  Shift shift_3 (.in_1(carry), .in_2(ARxBR_hi), .Output(hi1));  // open: Output0
  Shift shift_4 (.in_1(carry2), .in_2(hi1), .Output(hi2));  // open: Output0
  Shifter #(.width(32), .shift("lr")) shifter_1 (.in(in_1), .\dist (5'b00001), .out(AR));
  Shifter #(.width(32), .shift("lr")) shifter_2 (.in(in_2), .\dist (5'b00001), .out(BR));
  Multiplier #(.width(32)) multiplier_1 (.a(AR), .b(BR), .out(ARxBR_low), .cout(ARxBR_hi));  // open: cin
  Adder #(.width(32)) adder_1 (.a(A_S2), .b(low2), .out(S_low1), .cout(C_S_low1));  // open: cin
  Adder #(.width(32)) adder_2 (.a(B_S1), .b(S_low1), .out(S_low2), .cout(C_S_low2));  // open: cin
  assign bit_extender_1_out = {{31{1'b0}}, S3};  // Bit_Extender bit_extender_1
  Adder #(.width(32)) adder_3 (.a(bit_extender_1_out), .b(S_low2), .out(low), .cout(C_S_low3));  // open: cin
  Shifter #(.width(32)) shifter_3 (.in(AR), .\dist (5'b00001), .out(AL));
  Shifter #(.width(32)) shifter_4 (.in(BR), .\dist (5'b00001), .out(BL));
  assign bit_extender_2_out = {{31{1'b0}}, C_S_low1};  // Bit_Extender bit_extender_2
  assign bit_extender_3_out = {{31{1'b0}}, C_S_low2};  // Bit_Extender bit_extender_3
  assign bit_extender_4_out = {{31{1'b0}}, C_S_low3};  // Bit_Extender bit_extender_4
  Multiplexer #(.width(32), .enable("false")) multiplexer_1 (.in0({32{1'b0}}), .in1(AL), .out(A_S2), .sel(in_2[0]));
  Multiplexer #(.width(32), .enable("false")) multiplexer_2 (.in0({32{1'b0}}), .in1(BL), .out(B_S1), .sel(in_1[0]));
  Adder #(.width(32)) adder_4 (.a(bit_extender_2_out), .b(hi2), .out(S_hi1));  // open: cin, cout
  Adder #(.width(32)) adder_5 (.a(bit_extender_3_out), .b(S_hi1), .out(S_hi2));  // open: cin, cout
  Adder #(.width(32)) adder_6 (.a(bit_extender_4_out), .b(S_hi2), .out(hi));  // open: cin, cout
  and and_1 (S3, in_1[0], in_2[0]);

  // Other names for the same wires on the sheet: A[31:0] = in_1; S1 = in_1[0]; B[31:0] = in_2; S2 = in_2[0];
  //   S_hi[31:0] = hi; S_low[31:0] = low
endmodule

module Shift (
  input  in_1,
  input  [31:0] in_2,
  output Output0,
  output [31:0] Output
);


  assign Output = {in_2[30:0], in_1};
  assign Output0 = in_2[31];
endmodule

module Branch_Control (
  input  [6:0] Branch_I,
  input  [31:0] Rs,
  input  ZERO,
  input  [31:0] PC,
  input  NEG,
  input  [31:0] Relativo,
  input  [27:0] Destino,
  output [31:0] Result
);

  wire beq_t, bgtz_t, blez_t, bltz_t, bne_t, or_1_out, or_2_out;
  wire [1:0] SEL;
  wire [31:0] PC_4, PC_4_REL, RESULT_t;

  and and_1 (beq_t, Branch_I[2], ZERO);
  and and_2 (bne_t, Branch_I[3], ~ZERO);  // AND_Gate
  and and_3 (blez_t, Branch_I[6], or_1_out);
  or or_1 (or_1_out, ZERO, NEG);
  or or_2 (or_2_out, beq_t, bne_t, blez_t, bgtz_t, bltz_t);
  and and_4 (bgtz_t, Branch_I[4], ~NEG, ~ZERO);  // AND_Gate
  Priority_Encoder #(.select(2)) priority_encoder_1 (
    .in0(1'b1), .in1(Branch_I[1]), .in2(Branch_I[0]), .in3(or_2_out), .out(SEL));  // open: gs, en_out, en_in
  and and_5 (bltz_t, ~ZERO, NEG, Branch_I[5]);  // AND_Gate
  Adder #(.width(32)) adder_1 (.a(PC), .b(32'h4), .out(PC_4));  // open: cin, cout
  Adder #(.width(32)) adder_2 (.a(PC_4), .b(Relativo), .out(PC_4_REL));  // open: cin, cout
  assign Result = RESULT_t;  // AND_Gate and_6, 32 bits wide AND_Gate
  Multiplexer #(.select(2), .width(32), .enable("false")) multiplexer_1 (
    .in0(PC_4), .in1(Rs), .in2({PC[31:28], Destino}), .in3(PC_4_REL), .out(RESULT_t), .sel(SEL));

  // Other names for the same wires on the sheet: J = Branch_I[0]; JR = Branch_I[1]; BEQ = Branch_I[2];
  //   BNE = Branch_I[3]; BGTZ = Branch_I[4]; BLTZ = Branch_I[5]; BLEZ = Branch_I[6];
  //   DESTINY_JUMP[31:0] = {PC[31:28], Destino}; RELATIVE[31:0] = Relativo

  // Notes on the sheet:
  //   PC SELECTOR
  //   INPUTS
  //   aproximacion a 4*x
  //   PC SELECTION
  //   BRANCH CONTROL
endmodule

module Datapath (
  input  [31:0] Memory_Data,
  input  [31:0] Data,
  input  clk,
  input  clr,
  input  EN,
  input  Write_Enable,
  input  Register_Data_Rt,
  input  Branch_EN,
  input  Execute,
  input  Load_Instruction,
  input  Save_Mem,
  input  [1:0] Adress_To_Memory,
  input  [6:0] kbd_data,
  input  kbd_aviable,
  output halt,
  output [2:0] SM_Instruction,
  output Kbd_Enable,
  output tty_enable,
  output [31:0] registro,
  output [31:0] Mem_Dir,
  output [6:0] tty_data
);

  wire and_1_out, inmediate, load_Rd, load_zero, logic_i, lw, mul_div, nop, or_1_out, or_2_out, pop, push,
       RF_zero, rnd_t, sign, sw, zero;
  wire [1:0] data_to_RF;
  wire [3:0] alu_operador;
  wire [4:0] Data_Address, multiplexer_11_out, Rd, Rs, Rt, SB;
  wire [6:0] Branch_Instruction;
  wire [27:0] destino;
  wire [31:0] a_op, B, bit_extender_1_out, branch_control_1_result, branch_op, Data_Input, hi, Hi_Out_RF,
       Instruction_2_q, kbd_data_t, l_op, lo, Lo_Out_RF, Memory_Data_t, multiplexer_4_out, multiplexer_5_out,
       multiplexer_6_out, multiplexer_7_out, multiplexer_9_out, PC, result_alu, Rnd, SP;
  wire [31:7] A;

  assign bit_extender_1_out = {{25{1'b0}}, kbd_data};  // Bit_Extender bit_extender_1
  Multiplexer #(.width(32), .enable("false")) multiplexer_1 (
    .in0({A, tty_data}), .in1(B), .out(registro), .sel(Register_Data_Rt));
  Multiplexer #(.width(32), .enable("false")) multiplexer_2 (
    .in0({32{1'b1}}), .in1(bit_extender_1_out), .out(kbd_data_t), .sel(kbd_aviable));
  Multiplexer #(.select(2), .width(32), .enable("false")) multiplexer_3 (
    .in0(SP), .in1(result_alu), .in2(PC), .out(Mem_Dir), .sel(Adress_To_Memory));  // open: in3
  Register #(.width(32), .trigger("high")) Instruction (
    .D(Memory_Data), .en(Save_Mem), .Q(Memory_Data_t), .clk(clk), .clr(clr));
  or or_1 (or_1_out, EN, Execute);
  Register #(.width(32), .trigger("high")) Instruction_2 (
    .D(Data), .en(Load_Instruction), .Q(Instruction_2_q), .clk(clk), .clr(clr));
  Multiplexer #(.width(32), .enable("false")) multiplexer_4 (
    .in0({32{1'b0}}), .in1(Instruction_2_q), .out(multiplexer_4_out), .sel(or_1_out));
  Multiplexer #(.width(32), .enable("false")) multiplexer_5 (
    .in0(a_op), .in1(l_op), .out(multiplexer_5_out), .sel(logic_i));
  Multiplexer #(.width(32), .enable("false")) multiplexer_6 (
    .in0(B), .in1(multiplexer_5_out), .out(multiplexer_6_out), .sel(inmediate));
  Instruction_Decoder instruction_decoder_1 (
    .Instruction(multiplexer_4_out), .nop(nop), .tty(tty_enable), .Branch__I(Branch_Instruction),
    .halt(halt), .rnd(rnd_t), .kbd(Kbd_Enable), .destino(destino), .Rs(Rs), .pop(pop), .push(push),
    .logic_i(logic_i), .Rt(Rt), .lw(lw), .sw(sw), .Rd(Rd), .mul_div(mul_div), .alu_operator(alu_operador),
    .load_zero(load_zero), .data_to_RF(data_to_RF), .RF_zero(RF_zero), .load_Rd(load_Rd),
    .inmediate(inmediate), .Logic_Op(l_op), .Aritmetic_Op(a_op), .Branch(branch_op),
    .SM_Instruction(SM_Instruction));
  ALU alu_1 (
    .A({A, tty_data}), .B(multiplexer_6_out), .R(result_alu), .S(alu_operador), .hi(hi), .zero(zero),
    .lo(lo), .neg(sign));
  // Probe on Branch_Instruction
  Branch_Control branch_control_1 (
    .Branch_I(Branch_Instruction), .Rs({A, tty_data}), .ZERO(zero), .PC(PC), .NEG(sign),
    .Relativo(branch_op), .Destino(destino), .Result(branch_control_1_result));
  Register #(.width(32)) u_PC (.D(branch_control_1_result), .en(Branch_EN), .Q(PC), .clk(clk), .clr(clr));
  Multiplexer #(.select(2), .width(32), .enable("false")) multiplexer_7 (
    .in0(result_alu), .in1(Hi_Out_RF), .in2(Lo_Out_RF), .in3(Memory_Data_t), .out(multiplexer_7_out),
    .sel(data_to_RF));
  // Probe on data_to_RF
  Multiplexer #(.width(5), .enable("false")) multiplexer_8 (.in0(Rt), .in1({5{1'b0}}), .out(SB), .sel(RF_zero));
  Register_File register_file_1 (
    .Clock(clk), .Rs(Rs), .Hi_in(hi), .Rt(SB), .Rd(Data_Address), .Lo_in(lo), .Write_Data(Data_Input),
    .Clear(clr), .Mul_Div(mul_div), .Hi_out(Hi_Out_RF), .Lo_out(Lo_Out_RF), .Read_Data_1({A, tty_data}),
    .Read_Data_2(B), .pop(pop), .push(push), .SP(SP), .EN(EN));
  Multiplexer #(.width(32), .enable("false")) multiplexer_9 (
    .in0(multiplexer_7_out), .in1(Rnd), .out(multiplexer_9_out), .sel(rnd_t));
  Multiplexer #(.width(32), .enable("false")) multiplexer_10 (
    .in0(multiplexer_9_out), .in1(kbd_data_t), .out(Data_Input), .sel(Kbd_Enable));
  Multiplexer #(.width(5), .enable("false")) multiplexer_11 (
    .in0(Rt), .in1(Rd), .out(multiplexer_11_out), .sel(load_Rd));
  Multiplexer #(.width(5), .enable("false")) multiplexer_12 (
    .in0(multiplexer_11_out), .in1({5{1'b0}}), .out(Data_Address), .sel(or_2_out));
  or or_2 (or_2_out, load_zero, and_1_out);
  and and_1 (and_1_out, ~Write_Enable, lw);  // AND_Gate
  Random #(.width(32)) Random_Generator (.clk(clk), .out(Rnd));  // open: next, clr

  // Other names for the same wires on the sheet: kbd = Kbd_Enable; Rt_Data = Register_Data_Rt; tty = tty_enable;
  //   A[6:0] = tty_data

  // Notes on the sheet:
  //   Input
  //   Output
endmodule

module Memory_Manager (
  input  CS,
  input  RST,
  input  CLK,
  input  CLR,
  input  R_W_Time_Selector,
  input  [3:0] Read_Time,
  input  [3:0] Write_Time,
  input  [31:0] Address_In,
  input  [31:0] Register,
  input  [31:0] RAM_out_0,
  input  [31:0] RAM_out_1,
  input  [31:0] RAM_out_2,
  input  [31:0] RAM_out_3,
  output [31:0] RAM_in_0,
  output [31:0] RAM_in_1,
  output [31:0] RAM_in_2,
  output [31:0] RAM_in_3,
  output [31:0] Out,
  output [3:0] RAM_massk,
  output [15:0] Address,
  output Ready,
  output Save
);

  wire [3:0] multiplexer_1_out;
  wire [31:0] demultiplexer_1_out1;

  Decoder #(.select(2), .enable("false")) decoder_1 (
    .out0(RAM_massk[0]), .out1(RAM_massk[1]), .out2(RAM_massk[2]), .out3(RAM_massk[3]), .sel(Address_In[3:2]));
  Demultiplexer #(.width(32), .enable("false")) demultiplexer_1 (
    .out1(demultiplexer_1_out1), .in({Register[7:0], Register[15:8], Register[23:16], Register[31:24]}),
    .sel(R_W_Time_Selector));  // open: out0
  Multiplexer #(.width(4)) multiplexer_1 (
    .in0(Read_Time), .in1(Write_Time), .out(multiplexer_1_out), .sel(R_W_Time_Selector));  // open: en
  Demultiplexer #(.select(2), .width(32), .enable("false")) demultiplexer_2 (
    .out0(RAM_in_0), .out1(RAM_in_1), .out2(RAM_in_2), .out3(RAM_in_3), .in(demultiplexer_1_out1),
    .sel(Address_In[3:2]));
  Cronometer cronometer_1 (.Start(CS), .CLK(CLK), .Time(multiplexer_1_out), .Salva(Save), .Reset(RST), .Ready(Ready));
  Multiplexer #(.select(2), .width(32), .enable("false")) multiplexer_2 (
    .in0(RAM_out_0), .in1(RAM_out_1), .in2(RAM_out_2), .in3(RAM_out_3),
    .out({Out[7:0], Out[15:8], Out[23:16], Out[31:24]}), .sel(Address_In[3:2]));

  assign Address = Address_In[19:4];

  // Other names for the same wires on the sheet: block[1:0] = Address_In[3:2]; ADDR[15:0] = Address_In[19:4];
  //   R_T[3:0] = Read_Time; R_W_TS = R_W_Time_Selector; RAM_input_0[31:0] = RAM_in_0; RAM_input_1[31:0] = RAM_in_1;
  //   RAM_input_2[31:0] = RAM_in_2; RAM_input_3[31:0] = RAM_in_3; RAM_mask[3:0] = RAM_massk; W_T[3:0] = Write_Time

  // Notes on the sheet:
  //   input
  //   Cronometer logic
  //   Writing
  //   Reading
  //   output
endmodule

module Cronometer (
  input  Start,
  input  CLK,
  input  [3:0] Time,
  input  Reset,
  output Ready,
  output Salva
);

  Counter #(.width(4), .max('hf)) counter_1 (
    .load(1'b1), .D(Time), .count(Start), .carry(Salva), .clk(CLK));  // open: Q, clr
  D_Flip_Flop #(.trigger("falling")) d_ff_1 (.clk(CLK), .D(Salva), .Q(Ready), .reset(Reset));  // open: Qn, preset, en
endmodule

module Control_Unit (
  input  Reset,
  input  CLK,
  input  Mem_End,
  input  [2:0] Instruction,
  input  halt,
  output CS,
  output R_W,
  output Load_Instruction,
  output EN_Datapath,
  output Execute,
  output [1:0] Adress_To_Memory,
  output Enable_Datapath_Branch,
  output Register_Data_Rt,
  output Enable_LW
);

  wire ALU_Add, ALU_Add_LW, CS_Instruction, CS_LW, CS_Pop, CS_Push, CS_SW, demultiplexer_1_out0,
       demultiplexer_1_out1, demultiplexer_3_out1, demultiplexer_6_out1, demultiplexer_7_out1,
       Enable_Datapath_Estrict, Enable_Datapath_LW, Enable_Datapath_Pop, Enable_Datapath_Push,
       Enable_Datapath_SW, execute_1, execute_2, execute_3, IDLE_q, not_1_out, or_1_out, or_3_out, or_6_out,
       or_8_out, or_9_out, or_10_out, SP_Add;

  D_Flip_Flop IDLE (.clk(CLK), .D(demultiplexer_1_out0), .Q(IDLE_q), .preset(Reset));  // open: Qn, en, reset
  or or_1 (or_1_out, IDLE_q, Enable_Datapath_Branch);
  or or_2 (SP_Add, execute_2, execute_3);
  Demultiplexer #(.enable("false")) demultiplexer_1 (
    .out0(demultiplexer_1_out0), .out1(demultiplexer_1_out1), .in(or_1_out), .sel(not_1_out));
  not not_1 (not_1_out, halt);
  or or_3 (or_3_out, CS_Instruction, demultiplexer_1_out1);
  or or_4 (ALU_Add, ALU_Add_LW, Register_Data_Rt);
  D_Flip_Flop #(.trigger("falling")) u_Load_Instruction (
    .clk(CLK), .D(or_3_out), .Q(Load_Instruction), .reset(Reset));  // open: Qn, preset, en
  Demultiplexer #(.enable("false")) demultiplexer_2 (
    .out0(CS_Instruction), .out1(execute_1), .in(Load_Instruction), .sel(Mem_End));
  or or_5 (EN_Datapath, Enable_Datapath_LW, Enable_Datapath_Pop, Enable_LW, Enable_Datapath_Estrict, Enable_Datapath_Push);
  or u_R_W (R_W, CS_Push, CS_SW);
  Demultiplexer #(.select(3), .enable("false")) demultiplexer_3 (
    .out0(Enable_Datapath_Estrict), .out1(demultiplexer_3_out1), .out2(Enable_Datapath_Push),
    .out3(Enable_Datapath_LW), .out4(Enable_Datapath_SW), .in(execute_1), .sel(Instruction));  // open: out5, out6, out7
  Priority_Encoder #(.select(2)) priority_encoder_1 (
    .in0(SP_Add), .in1(ALU_Add), .in2(Load_Instruction), .out(Adress_To_Memory));  // open: in3, gs, en_out, en_in
  D_Flip_Flop #(.trigger("falling")) Read (
    .clk(CLK), .D(or_6_out), .Q(execute_2), .reset(Reset));  // open: Qn, preset, en
  or or_6 (or_6_out, CS_Pop, demultiplexer_3_out1);
  or or_7 (CS, CS_Instruction, CS_Pop, CS_Push, CS_LW, CS_SW);
  Demultiplexer #(.enable("false")) demultiplexer_4 (
    .out0(CS_Pop), .out1(Enable_Datapath_Pop), .in(execute_2), .sel(Mem_End));
  or or_8 (or_8_out, CS_Push, Enable_Datapath_Push);
  or or_9 (or_9_out, CS_LW, Enable_Datapath_LW);
  or or_10 (or_10_out, CS_SW, Enable_Datapath_SW);
  D_Flip_Flop #(.trigger("falling")) Write (
    .clk(CLK), .D(or_8_out), .Q(execute_3), .reset(Reset));  // open: Qn, preset, en
  D_Flip_Flop #(.trigger("falling")) Write_2 (
    .clk(CLK), .D(or_9_out), .Q(ALU_Add_LW), .reset(Reset));  // open: Qn, preset, en
  D_Flip_Flop #(.trigger("falling")) Write_3 (
    .clk(CLK), .D(or_10_out), .Q(Register_Data_Rt), .reset(Reset));  // open: Qn, preset, en
  Demultiplexer #(.enable("false")) demultiplexer_5 (.out0(CS_LW), .out1(Enable_LW), .in(ALU_Add_LW), .sel(Mem_End));
  Demultiplexer #(.enable("false")) demultiplexer_6 (
    .out0(CS_SW), .out1(demultiplexer_6_out1), .in(Register_Data_Rt), .sel(Mem_End));
  or or_11 (Execute, execute_1, execute_2, execute_3, ALU_Add_LW, Register_Data_Rt);
  Demultiplexer #(.enable("false")) demultiplexer_7 (
    .out0(CS_Push), .out1(demultiplexer_7_out1), .in(execute_3), .sel(Mem_End));
  or or_12 (Enable_Datapath_Branch, Enable_Datapath_Pop, demultiplexer_7_out1, Enable_LW, Enable_Datapath_Estrict, demultiplexer_6_out1);

  // Other names for the same wires on the sheet: Enable_Datapath = EN_Datapath; Enable_Datapath_LW2 = Enable_LW;
  //   End = Enable_Datapath_Branch; SP_Add_Pop = execute_2; SP_Add_Push = execute_3; execute_4 = ALU_Add_LW;
  //   ALU_Add_SW = Register_Data_Rt; execute_5 = Register_Data_Rt; PC_Add = Load_Instruction; R_W_Push = CS_Push;
  //   R_W_SW = CS_SW

  // Notes on the sheet:
  //   Ouput Data
  //   Input Data
  //   Managing Repetitions of Signals
  //   State Machine
  //   POP
  //   PUSH
  //   LW
  //   SW
  //   Estrict Datapath Operation
endmodule
